// Logisim project cpu16.circ as structural Verilog: 50 circuits, main circuit main
module main (
);

  wire cpu_1_clk_out, cpu_1_dbus_rw, decoder_1_out0, decoder_1_out1, decoder_1_out2, decoder_1_out3,
       mmu_1_io_on, mmu_1_mem_on;
  wire [3:0] mmu_1_io_addr;
  wire [15:0] controlled_buffer_1_out, cpu_1_addrbus_out, cpu_1_dbus_out, mmu_1_memaddr, ram_1_dout;

  // Probe on cpu_1_addrbus_out
  CPU cpu_1 (
    .dbus_in(controlled_buffer_1_out), .dbus_out(cpu_1_dbus_out), .dbus_rw(cpu_1_dbus_rw),
    .CLK_out(cpu_1_clk_out), .addrbus_out(cpu_1_addrbus_out));
  MMU mmu_1 (
    .addr(cpu_1_addrbus_out), .memaddr(mmu_1_memaddr), .io_addr(mmu_1_io_addr), .mem_on(mmu_1_mem_on),
    .io_on(mmu_1_io_on));
  // Probe on cpu_1_dbus_out
  assign controlled_buffer_1_out = mmu_1_mem_on ? ram_1_dout : 16'bz;  // Controlled_Buffer controlled_buffer_1
  // Probe on mmu_1_memaddr
  Decoder #(.select(3)) decoder_1 (
    .out0(decoder_1_out0), .out1(decoder_1_out1), .out2(decoder_1_out2), .out3(decoder_1_out3),
    .sel(mmu_1_io_addr[3:1]), .en(mmu_1_io_on));  // open: out4, out5, out6, out7
  RAM #(.addrWidth(16), .dataWidth(16), .enables("line"), .trigger("falling")) ram_1 (
    .addr(mmu_1_memaddr), .we(cpu_1_dbus_rw), .clk(cpu_1_clk_out), .din(cpu_1_dbus_out), .dout(ram_1_dout));
  // Probe on ram_1_dout
  IO_port io_port_1 (
    .clk(cpu_1_clk_out), .rw(cpu_1_dbus_rw), .addr(mmu_1_io_addr[0]), .cpu_select(decoder_1_out0),
    .cpu_in(cpu_1_dbus_out), .cpu_out(controlled_buffer_1_out));  // open: io_in, io_out
  IO_port io_port_2 (
    .clk(cpu_1_clk_out), .rw(cpu_1_dbus_rw), .addr(mmu_1_io_addr[0]), .cpu_select(decoder_1_out1),
    .cpu_in(cpu_1_dbus_out), .cpu_out(controlled_buffer_1_out));  // open: io_in, io_out
  IO_port io_port_3 (
    .clk(cpu_1_clk_out), .rw(cpu_1_dbus_rw), .addr(mmu_1_io_addr[0]), .cpu_select(decoder_1_out2),
    .cpu_in(cpu_1_dbus_out), .cpu_out(controlled_buffer_1_out));  // open: io_in, io_out
  IO_port io_port_4 (
    .clk(cpu_1_clk_out), .rw(cpu_1_dbus_rw), .addr(mmu_1_io_addr[0]), .cpu_select(decoder_1_out3),
    .cpu_in(cpu_1_dbus_out), .cpu_out(controlled_buffer_1_out));  // open: io_in, io_out

  // Notes on the sheet:
  //   IO bus
endmodule

module ALU_AND (
  input  [15:0] in_A,
  input  [15:0] in_B,
  output [15:0] out_A
);

  and and_1 (out_A[0], in_A[0], in_B[0]);
  and and_2 (out_A[1], in_A[1], in_B[1]);
  and and_3 (out_A[2], in_A[2], in_B[2]);
  and and_4 (out_A[3], in_A[3], in_B[3]);
  and and_5 (out_A[4], in_A[4], in_B[4]);
  and and_6 (out_A[5], in_A[5], in_B[5]);
  and and_7 (out_A[6], in_A[6], in_B[6]);
  and and_8 (out_A[7], in_A[7], in_B[7]);
  and and_9 (out_A[8], in_A[8], in_B[8]);
  and and_10 (out_A[9], in_A[9], in_B[9]);
  and and_11 (out_A[10], in_A[10], in_B[10]);
  and and_12 (out_A[11], in_A[11], in_B[11]);
  and and_13 (out_A[12], in_A[12], in_B[12]);
  and and_14 (out_A[13], in_A[13], in_B[13]);
  and and_15 (out_A[14], in_A[14], in_B[14]);
  and and_16 (out_A[15], in_A[15], in_B[15]);
endmodule

module ALU_OR (
  input  [15:0] in_A,
  input  [15:0] in_B,
  output [15:0] out_A
);

  or or_1 (out_A[0], in_A[0], in_B[0]);
  or or_2 (out_A[1], in_A[1], in_B[1]);
  or or_3 (out_A[2], in_A[2], in_B[2]);
  or or_4 (out_A[3], in_A[3], in_B[3]);
  or or_5 (out_A[4], in_A[4], in_B[4]);
  or or_6 (out_A[5], in_A[5], in_B[5]);
  or or_7 (out_A[6], in_A[6], in_B[6]);
  or or_8 (out_A[7], in_A[7], in_B[7]);
  or or_9 (out_A[8], in_A[8], in_B[8]);
  or or_10 (out_A[9], in_A[9], in_B[9]);
  or or_11 (out_A[10], in_A[10], in_B[10]);
  or or_12 (out_A[11], in_A[11], in_B[11]);
  or or_13 (out_A[12], in_A[12], in_B[12]);
  or or_14 (out_A[13], in_A[13], in_B[13]);
  or or_15 (out_A[14], in_A[14], in_B[14]);
  or or_16 (out_A[15], in_A[15], in_B[15]);
endmodule

module ALU_XOR (
  input  [15:0] in_A,
  input  [15:0] in_B,
  output [15:0] out_A
);

  xor xor_1 (out_A[0], in_A[0], in_B[0]);
  xor xor_2 (out_A[1], in_A[1], in_B[1]);
  xor xor_3 (out_A[2], in_A[2], in_B[2]);
  xor xor_4 (out_A[3], in_A[3], in_B[3]);
  xor xor_5 (out_A[4], in_A[4], in_B[4]);
  xor xor_6 (out_A[5], in_A[5], in_B[5]);
  xor xor_7 (out_A[6], in_A[6], in_B[6]);
  xor xor_8 (out_A[7], in_A[7], in_B[7]);
  xor xor_9 (out_A[8], in_A[8], in_B[8]);
  xor xor_10 (out_A[9], in_A[9], in_B[9]);
  xor xor_11 (out_A[10], in_A[10], in_B[10]);
  xor xor_12 (out_A[11], in_A[11], in_B[11]);
  xor xor_13 (out_A[12], in_A[12], in_B[12]);
  xor xor_14 (out_A[13], in_A[13], in_B[13]);
  xor xor_15 (out_A[14], in_A[14], in_B[14]);
  xor xor_16 (out_A[15], in_A[15], in_B[15]);
endmodule

module ALU (
  input  [15:0] reg_a,
  input  [15:0] reg_b,
  input  [3:0] ALU_select,
  input  EFLAGS_write,
  input  CLK,
  output [15:0] alu_out,
  output [15:0] EFLAGS_out
);

  wire and_1_out, and_2_out, and_3_out, and_4_out, and_5_out, and_6_out, comparator_1_eq, comparator_1_gt,
       comparator_1_lt, eqx4_1_eq, flagout_1_neg, flagout_1_pos, flagout_1_zero, not_2_out;
  wire [2:0] or_3_out;
  wire [3:0] bit_extender_1_out;
  wire [15:0] adder_1_out, alu_and_1_out_a, alu_or_1_out_a, alu_xor_1_out_a, multiplier_1_out, not_1_out,
       shifter_1_out, shifter_2_out, shifter_3_out, subtractor_1_out;

  Bit_Extender #(.in_width(16), .out_width(4), .\type ("zero")) bit_extender_1 (.in(reg_b), .out(bit_extender_1_out));
  ALU_AND alu_and_1 (.in_A(reg_a), .in_B(reg_b), .out_A(alu_and_1_out_a));
  ALU_OR alu_or_1 (.in_A(reg_a), .in_B(reg_b), .out_A(alu_or_1_out_a));
  ALU_XOR alu_xor_1 (.in_A(reg_a), .in_B(reg_b), .out_A(alu_xor_1_out_a));
  Adder #(.width(16)) adder_1 (.a(reg_a), .b(reg_b), .out(adder_1_out));  // open: cin, cout
  Subtractor #(.width(16)) subtractor_1 (.a(reg_a), .b(reg_b), .out(subtractor_1_out));  // open: bin, bout
  Multiplier #(.width(16)) multiplier_1 (.a(reg_a), .b(reg_b), .out(multiplier_1_out));  // open: cin, cout
  Shifter #(.width(16)) shifter_1 (.in(reg_a), .\dist (bit_extender_1_out), .out(shifter_1_out));
  Shifter #(.shift("ar"), .width(16)) shifter_2 (.in(reg_a), .\dist (bit_extender_1_out), .out(shifter_2_out));
  Shifter #(.shift("lr"), .width(16)) shifter_3 (.in(reg_a), .\dist (bit_extender_1_out), .out(shifter_3_out));
  assign not_1_out = ~reg_a;  // NOT_Gate not_1, 16 bits wide
  Comparator #(.width(16)) comparator_1 (
    .a(reg_a), .b(reg_b), .gt(comparator_1_gt), .eq(comparator_1_eq), .lt(comparator_1_lt));
  Multiplexer #(.select(4), .width(16)) multiplexer_1 (
    .in0(alu_and_1_out_a), .in1(alu_or_1_out_a), .in2(alu_xor_1_out_a), .in3(adder_1_out),
    .in4(subtractor_1_out), .in5(multiplier_1_out), .in6(shifter_1_out), .in7(shifter_2_out),
    .in8(shifter_3_out), .in9(not_1_out), .out(alu_out), .sel(ALU_select));  // open: in10, in11, in12, in13, in14, in15
  Eqx4 eqx4_1 (.inA(ALU_select), .inB(4'b1111), .eq(eqx4_1_eq));
  and and_1 (and_1_out, eqx4_1_eq, comparator_1_lt);
  and and_2 (and_2_out, eqx4_1_eq, comparator_1_eq);
  FlagOut flagout_1 (.in16(alu_out), .zero(flagout_1_zero), .pos(flagout_1_pos), .neg(flagout_1_neg));
  not not_2 (not_2_out, eqx4_1_eq);
  and and_3 (and_3_out, eqx4_1_eq, comparator_1_gt);
  and and_4 (and_4_out, not_2_out, flagout_1_neg);
  or or_1 (or_3_out[2], and_4_out, and_1_out);
  Register register_1 (.D({{5{1'b0}}, or_3_out}), .en(EFLAGS_write), .clk(CLK), .Q(EFLAGS_out[7:0]));  // open: clr
  and and_5 (and_5_out, not_2_out, flagout_1_zero);
  and and_6 (and_6_out, not_2_out, flagout_1_pos);
  or or_2 (or_3_out[1], and_2_out, and_5_out);
  or or_3 (or_3_out[0], and_3_out, and_6_out);

  assign EFLAGS_out[15:8] = {8{1'b0}};

  // Notes on the sheet:
  //   output data line
  //   CMP constant
  //   N Z P X X X X X
  //   EFLAGS 0-8
endmodule

module D_latch (
  input  D,
  input  E,
  output O,
  output O_inv
);

  wire and_1_out, and_2_out, not_1_out, or_1_out, or_2_out;

  not not_1 (not_1_out, D);
  and and_1 (and_1_out, not_1_out, E);
  and and_2 (and_2_out, E, D);
  LED led_1 (.in(O));
  or or_1 (or_1_out, and_1_out, O_inv);
  not not_2 (O, or_1_out);
  or or_2 (or_2_out, O, and_2_out);
  not not_3 (O_inv, or_2_out);
endmodule

module D_FF_rising (
  input  D,
  input  CLK,
  output O_inv,
  output O
);

  wire and_1_out, and_2_out, and_3_out, and_4_out, not_1_out, not_2_out, not_3_out, not_4_out, not_5_out,
       or_1_out, or_2_out;

  not not_1 (not_1_out, CLK);
  not not_2 (not_2_out, D);
  and and_1 (and_1_out, not_2_out, not_1_out);
  and and_2 (and_2_out, not_1_out, D);
  not not_3 (not_3_out, or_1_out);
  or or_1 (or_1_out, and_1_out, not_4_out);
  or or_2 (or_2_out, not_3_out, and_2_out);
  not not_4 (not_4_out, or_2_out);
  and and_3 (and_3_out, not_3_out, not_5_out);
  not not_5 (not_5_out, not_1_out);
  and and_4 (and_4_out, not_5_out, not_4_out);
  LED led_1 (.in(O_inv));
  nor nor_1 (O_inv, and_3_out, O);
  nor nor_2 (O, O_inv, and_4_out);
endmodule

module D_FF_falling (
  input  D,
  input  CLK,
  output O_inv,
  output O
);

  wire and_1_out, and_2_out, and_3_out, and_4_out, not_1_out, not_2_out, not_3_out, not_4_out, or_1_out,
       or_2_out;

  not not_1 (not_1_out, D);
  and and_1 (and_1_out, not_1_out, CLK);
  and and_2 (and_2_out, CLK, D);
  not not_2 (not_2_out, or_1_out);
  or or_1 (or_1_out, and_1_out, not_3_out);
  or or_2 (or_2_out, not_2_out, and_2_out);
  not not_3 (not_3_out, or_2_out);
  and and_3 (and_3_out, not_2_out, not_4_out);
  not not_4 (not_4_out, CLK);
  and and_4 (and_4_out, not_4_out, not_3_out);
  LED led_1 (.in(O_inv));
  nor nor_1 (O_inv, and_3_out, O);
  nor nor_2 (O, O_inv, and_4_out);
endmodule

module SR_latch (
  input  D,
  input  E,
  input  in_3,
  output O,
  output O_inv
);

  wire and_1_out, and_2_out, clock_1_out, d_ff_1_q, d_latch_1_o, not_1_out, or_1_out, or_2_out;

  not not_1 (not_1_out, D);
  and and_1 (and_1_out, not_1_out, E);
  or or_1 (or_1_out, and_1_out, O_inv);
  not not_2 (O, or_1_out);
  or or_2 (or_2_out, O, and_2_out);
  not not_3 (O_inv, or_2_out);
  and and_2 (and_2_out, E, D);
  Clock clock_1 (.out(clock_1_out));
  LED led_1 (.in(O));
  D_Flip_Flop d_ff_1 (.clk(clock_1_out), .D(in_3), .Q(d_ff_1_q));  // open: Qn, preset, reset
  D_latch d_latch_1 (.E(clock_1_out), .D(in_3), .O(d_latch_1_o));  // open: O_inv
  LED led_2 (.in(d_ff_1_q));
  LED led_3 (.in(d_latch_1_o));
endmodule

module GPREG (
  input  [15:0] D,
  input  WRITE_ENABLE,
  input  ENABLE,
  output [15:0] O
);

  wire and_1_out, d_latch_1_o, d_latch_2_o, d_latch_3_o, d_latch_4_o, d_latch_5_o, d_latch_6_o, d_latch_7_o,
       d_latch_8_o, d_latch_9_o, d_latch_10_o, d_latch_11_o, d_latch_12_o, d_latch_13_o, d_latch_14_o,
       d_latch_15_o, d_latch_16_o;

  and and_1 (and_1_out, WRITE_ENABLE, ENABLE);
  D_latch d_latch_1 (.E(and_1_out), .D(D[0]), .O(d_latch_1_o));  // open: O_inv
  D_latch d_latch_2 (.E(and_1_out), .D(D[1]), .O(d_latch_2_o));  // open: O_inv
  D_latch d_latch_3 (.E(and_1_out), .D(D[2]), .O(d_latch_3_o));  // open: O_inv
  D_latch d_latch_4 (.E(and_1_out), .D(D[3]), .O(d_latch_4_o));  // open: O_inv
  D_latch d_latch_5 (.E(and_1_out), .D(D[4]), .O(d_latch_5_o));  // open: O_inv
  D_latch d_latch_6 (.E(and_1_out), .D(D[5]), .O(d_latch_6_o));  // open: O_inv
  D_latch d_latch_7 (.E(and_1_out), .D(D[6]), .O(d_latch_7_o));  // open: O_inv
  D_latch d_latch_8 (.E(and_1_out), .D(D[7]), .O(d_latch_8_o));  // open: O_inv
  D_latch d_latch_9 (.E(and_1_out), .D(D[8]), .O(d_latch_9_o));  // open: O_inv
  D_latch d_latch_10 (.E(and_1_out), .D(D[9]), .O(d_latch_10_o));  // open: O_inv
  D_latch d_latch_11 (.E(and_1_out), .D(D[10]), .O(d_latch_11_o));  // open: O_inv
  D_latch d_latch_12 (.E(and_1_out), .D(D[11]), .O(d_latch_12_o));  // open: O_inv
  D_latch d_latch_13 (.E(and_1_out), .D(D[12]), .O(d_latch_13_o));  // open: O_inv
  D_latch d_latch_14 (.E(and_1_out), .D(D[13]), .O(d_latch_14_o));  // open: O_inv
  D_latch d_latch_15 (.E(and_1_out), .D(D[14]), .O(d_latch_15_o));  // open: O_inv
  D_latch d_latch_16 (.E(and_1_out), .D(D[15]), .O(d_latch_16_o));  // open: O_inv
  and and_2 (O[0], d_latch_1_o, ENABLE);
  and and_3 (O[1], d_latch_2_o, ENABLE);
  and and_4 (O[2], d_latch_3_o, ENABLE);
  and and_5 (O[3], d_latch_4_o, ENABLE);
  and and_6 (O[4], d_latch_5_o, ENABLE);
  and and_7 (O[5], d_latch_6_o, ENABLE);
  and and_8 (O[6], d_latch_7_o, ENABLE);
  and and_9 (O[7], d_latch_8_o, ENABLE);
  and and_10 (O[8], d_latch_9_o, ENABLE);
  and and_11 (O[9], d_latch_10_o, ENABLE);
  and and_12 (O[10], d_latch_11_o, ENABLE);
  and and_13 (O[11], d_latch_12_o, ENABLE);
  and and_14 (O[12], d_latch_13_o, ENABLE);
  and and_15 (O[13], d_latch_14_o, ENABLE);
  and and_16 (O[14], d_latch_15_o, ENABLE);
  and and_17 (O[15], d_latch_16_o, ENABLE);
endmodule

module GPREG_2 (
  input  [15:0] D,
  input  WRITE_ENABLE,
  input  ENABLE,
  output [15:0] O
);

  wire and_1_out;

  and and_1 (and_1_out, WRITE_ENABLE, ENABLE);
  D_latch d_latch_1 (.E(and_1_out), .D(D[0]), .O(O[0]));  // open: O_inv
  D_latch d_latch_2 (.E(and_1_out), .D(D[1]), .O(O[1]));  // open: O_inv
  D_latch d_latch_3 (.E(and_1_out), .D(D[2]), .O(O[2]));  // open: O_inv
  D_latch d_latch_4 (.E(and_1_out), .D(D[3]), .O(O[3]));  // open: O_inv
  D_latch d_latch_5 (.E(and_1_out), .D(D[4]), .O(O[4]));  // open: O_inv
  D_latch d_latch_6 (.E(and_1_out), .D(D[5]), .O(O[5]));  // open: O_inv
  D_latch d_latch_7 (.E(and_1_out), .D(D[6]), .O(O[6]));  // open: O_inv
  D_latch d_latch_8 (.E(and_1_out), .D(D[7]), .O(O[7]));  // open: O_inv
  D_latch d_latch_9 (.E(and_1_out), .D(D[8]), .O(O[8]));  // open: O_inv
  D_latch d_latch_10 (.E(and_1_out), .D(D[9]), .O(O[9]));  // open: O_inv
  D_latch d_latch_11 (.E(and_1_out), .D(D[10]), .O(O[10]));  // open: O_inv
  D_latch d_latch_12 (.E(and_1_out), .D(D[11]), .O(O[11]));  // open: O_inv
  D_latch d_latch_13 (.E(and_1_out), .D(D[12]), .O(O[12]));  // open: O_inv
  D_latch d_latch_14 (.E(and_1_out), .D(D[13]), .O(O[13]));  // open: O_inv
  D_latch d_latch_15 (.E(and_1_out), .D(D[14]), .O(O[14]));  // open: O_inv
  D_latch d_latch_16 (.E(and_1_out), .D(D[15]), .O(O[15]));  // open: O_inv
endmodule

module GPREG_3 (
  input  [15:0] D,
  input  WRITE_ENABLE,
  input  ENABLE,
  output [15:0] O
);

  wire and_1_out;

  and and_1 (and_1_out, WRITE_ENABLE, ENABLE);
  D_Flip_Flop d_ff_1 (.clk(and_1_out), .D(D[0]), .Q(O[0]));  // open: Qn, preset, reset
  D_Flip_Flop d_ff_2 (.clk(and_1_out), .D(D[1]), .Q(O[1]));  // open: Qn, preset, reset
  D_Flip_Flop d_ff_3 (.clk(and_1_out), .D(D[2]), .Q(O[2]));  // open: Qn, preset, reset
  D_Flip_Flop d_ff_4 (.clk(and_1_out), .D(D[3]), .Q(O[3]));  // open: Qn, preset, reset
  D_Flip_Flop d_ff_5 (.clk(and_1_out), .D(D[4]), .Q(O[4]));  // open: Qn, preset, reset
  D_Flip_Flop d_ff_6 (.clk(and_1_out), .D(D[5]), .Q(O[5]));  // open: Qn, preset, reset
  D_Flip_Flop d_ff_7 (.clk(and_1_out), .D(D[6]), .Q(O[6]));  // open: Qn, preset, reset
  D_Flip_Flop d_ff_8 (.clk(and_1_out), .D(D[7]), .Q(O[7]));  // open: Qn, preset, reset
  D_Flip_Flop d_ff_9 (.clk(and_1_out), .D(D[8]), .Q(O[8]));  // open: Qn, preset, reset
  D_Flip_Flop d_ff_10 (.clk(and_1_out), .D(D[9]), .Q(O[9]));  // open: Qn, preset, reset
  D_Flip_Flop d_ff_11 (.clk(and_1_out), .D(D[10]), .Q(O[10]));  // open: Qn, preset, reset
  D_Flip_Flop d_ff_12 (.clk(and_1_out), .D(D[11]), .Q(O[11]));  // open: Qn, preset, reset
  D_Flip_Flop d_ff_13 (.clk(and_1_out), .D(D[12]), .Q(O[12]));  // open: Qn, preset, reset
  D_Flip_Flop d_ff_14 (.clk(and_1_out), .D(D[13]), .Q(O[13]));  // open: Qn, preset, reset
  D_Flip_Flop d_ff_15 (.clk(and_1_out), .D(D[14]), .Q(O[14]));  // open: Qn, preset, reset
  D_Flip_Flop d_ff_16 (.clk(and_1_out), .D(D[15]), .Q(O[15]));  // open: Qn, preset, reset
endmodule

module GPREG_BANK (
  input  [2:0] write_sel,
  input  write_enable,
  input  [2:0] read2_sel,
  input  read2_en,
  input  CLK,
  input  [15:0] write_i,
  input  [2:0] read1_sel,
  input  read1_en,
  output [15:0] read2_o,
  output [15:0] read1_o
);

  wire decoder_1_out0, decoder_1_out1, decoder_1_out2, decoder_1_out3, decoder_1_out4, decoder_1_out5,
       decoder_1_out6, decoder_1_out7;
  wire [15:0] gpreg_3_1_o, gpreg_3_2_o, gpreg_3_3_o, gpreg_3_4_o, gpreg_3_5_o, gpreg_3_6_o, gpreg_3_7_o,
       gpreg_3_8_o, multiplexer_1_out, multiplexer_2_out;

  Decoder #(.select(3)) decoder_1 (
    .out0(decoder_1_out0), .out1(decoder_1_out1), .out2(decoder_1_out2), .out3(decoder_1_out3),
    .out4(decoder_1_out4), .out5(decoder_1_out5), .out6(decoder_1_out6), .out7(decoder_1_out7),
    .sel(write_sel), .en(write_enable));
  GPREG_3 gpreg_3_1 (.D(write_i), .WRITE_ENABLE(decoder_1_out0), .ENABLE(CLK), .O(gpreg_3_1_o));
  GPREG_3 gpreg_3_2 (.D(write_i), .WRITE_ENABLE(decoder_1_out2), .ENABLE(CLK), .O(gpreg_3_2_o));
  GPREG_3 gpreg_3_3 (.D(write_i), .WRITE_ENABLE(decoder_1_out4), .ENABLE(CLK), .O(gpreg_3_3_o));
  GPREG_3 gpreg_3_4 (.D(write_i), .WRITE_ENABLE(decoder_1_out6), .ENABLE(CLK), .O(gpreg_3_4_o));
  GPREG_3 gpreg_3_5 (.D(write_i), .WRITE_ENABLE(decoder_1_out1), .ENABLE(CLK), .O(gpreg_3_5_o));
  GPREG_3 gpreg_3_6 (.D(write_i), .WRITE_ENABLE(decoder_1_out3), .ENABLE(CLK), .O(gpreg_3_6_o));
  GPREG_3 gpreg_3_7 (.D(write_i), .WRITE_ENABLE(decoder_1_out5), .ENABLE(CLK), .O(gpreg_3_7_o));
  GPREG_3 gpreg_3_8 (.D(write_i), .WRITE_ENABLE(decoder_1_out7), .ENABLE(CLK), .O(gpreg_3_8_o));
  Multiplexer #(.enable("true"), .select(3), .width(16)) multiplexer_1 (
    .in0(gpreg_3_1_o), .in1(gpreg_3_5_o), .in2(gpreg_3_2_o), .in3(gpreg_3_6_o), .in4(gpreg_3_3_o),
    .in5(gpreg_3_7_o), .in6(gpreg_3_4_o), .in7(gpreg_3_8_o), .out(multiplexer_1_out), .sel(read2_sel),
    .en(read2_en));
  Multiplexer #(.enable("true"), .select(3), .width(16)) multiplexer_2 (
    .in0(gpreg_3_1_o), .in1(gpreg_3_5_o), .in2(gpreg_3_2_o), .in3(gpreg_3_6_o), .in4(gpreg_3_3_o),
    .in5(gpreg_3_7_o), .in6(gpreg_3_4_o), .in7(gpreg_3_8_o), .out(multiplexer_2_out), .sel(read1_sel),
    .en(read1_en));
  // Probe on gpreg_3_1_o
  // Probe on gpreg_3_5_o
  // Probe on gpreg_3_2_o
  // Probe on gpreg_3_6_o
  // Probe on gpreg_3_3_o
  // Probe on gpreg_3_7_o
  // Probe on gpreg_3_4_o
  // Probe on gpreg_3_8_o
  assign read2_o = read2_en ? multiplexer_1_out : 16'bz;  // Controlled_Buffer controlled_buffer_1
  assign read1_o = read1_en ? multiplexer_2_out : 16'bz;  // Controlled_Buffer controlled_buffer_2
endmodule

module GPREG_BANK2 (
  input  [2:0] write_sel,
  input  write_enable,
  input  [2:0] read2_sel,
  input  read2_en,
  input  CLK,
  input  [15:0] write_i,
  input  [2:0] read1_sel,
  input  read1_en,
  output [15:0] read2_o,
  output [15:0] read1_o
);

  wire decoder_1_out0, decoder_1_out1, decoder_1_out2, decoder_1_out3, decoder_1_out4, decoder_1_out5,
       decoder_1_out6, decoder_1_out7;
  wire [15:0] gpreg_2_1_o, gpreg_2_2_o, gpreg_2_3_o, gpreg_2_4_o, gpreg_2_5_o, gpreg_2_6_o, gpreg_2_7_o,
       gpreg_2_8_o;

  Decoder #(.select(3)) decoder_1 (
    .out0(decoder_1_out0), .out1(decoder_1_out1), .out2(decoder_1_out2), .out3(decoder_1_out3),
    .out4(decoder_1_out4), .out5(decoder_1_out5), .out6(decoder_1_out6), .out7(decoder_1_out7),
    .sel(write_sel), .en(write_enable));
  GPREG_2 gpreg_2_1 (.WRITE_ENABLE(decoder_1_out0), .ENABLE(CLK), .D(write_i), .O(gpreg_2_1_o));
  GPREG_2 gpreg_2_2 (.WRITE_ENABLE(decoder_1_out2), .ENABLE(CLK), .D(write_i), .O(gpreg_2_2_o));
  GPREG_2 gpreg_2_3 (.WRITE_ENABLE(decoder_1_out4), .ENABLE(CLK), .D(write_i), .O(gpreg_2_3_o));
  GPREG_2 gpreg_2_4 (.WRITE_ENABLE(decoder_1_out6), .ENABLE(CLK), .D(write_i), .O(gpreg_2_4_o));
  GPREG_2 gpreg_2_5 (.WRITE_ENABLE(decoder_1_out7), .ENABLE(CLK), .D(write_i), .O(gpreg_2_5_o));
  GPREG_2 gpreg_2_6 (.WRITE_ENABLE(decoder_1_out1), .ENABLE(CLK), .D(write_i), .O(gpreg_2_6_o));
  GPREG_2 gpreg_2_7 (.WRITE_ENABLE(decoder_1_out3), .ENABLE(CLK), .D(write_i), .O(gpreg_2_7_o));
  GPREG_2 gpreg_2_8 (.WRITE_ENABLE(decoder_1_out5), .ENABLE(CLK), .D(write_i), .O(gpreg_2_8_o));
  Multiplexer #(.enable("true"), .select(3), .width(16)) multiplexer_1 (
    .in0(gpreg_2_1_o), .in1(gpreg_2_6_o), .in2(gpreg_2_2_o), .in3(gpreg_2_7_o), .in4(gpreg_2_3_o),
    .in5(gpreg_2_8_o), .in6(gpreg_2_4_o), .in7(gpreg_2_5_o), .out(read2_o), .sel(read2_sel), .en(read2_en));
  Multiplexer #(.enable("true"), .select(3), .width(16)) multiplexer_2 (
    .in0(gpreg_2_1_o), .in1(gpreg_2_6_o), .in2(gpreg_2_2_o), .in3(gpreg_2_7_o), .in4(gpreg_2_3_o),
    .in5(gpreg_2_8_o), .in6(gpreg_2_4_o), .in7(gpreg_2_5_o), .out(read1_o), .sel(read1_sel), .en(read1_en));
endmodule

module CU_Splitter (
  input  [15:0] IR,
  input  immselectable,
  input  [1:0] immctl,
  input  [2:0] regabctl,
  input  [1:0] regwctl,
  output [4:0] Opcode,
  output [15:0] immediate,
  output W_en,
  output [2:0] RB,
  output [15:0] flags_direct,
  output RA_en,
  output RB_en,
  output [2:0] RW,
  output [2:0] RA
);

  wire and_1_out, and_2_out, and_4_out, decoder_1_out1, decoder_1_out2, decoder_1_out3, decoder_1_out4,
       decoder_2_out1, decoder_2_out2, decoder_2_out3, decoder_3_out0, decoder_3_out1, decoder_3_out2,
       decoder_3_out3, not_1_out, not_2_out, not_3_out, not_4_out, or_1_out, or_4_out;
  wire [2:0] three_one_and_1_out3, three_one_and_2_out3, three_one_and_4_out3, three_one_and_5_out3,
       three_one_and_6_out3, three_one_and_7_out3;
  wire [15:0] bit_extender_1_out, bit_extender_2_out, bit_extender_3_out, bit_extender_4_out,
       bit_extender_5_out, bit_extender_6_out, multiplexer_1_out, multiplexer_2_out, multiplexer_4_out;

  PLA pla_1 ();  // open: in, out
  assign bit_extender_1_out = {{11{1'b0}}, IR[4:0]};  // Bit_Extender bit_extender_1
  Multiplexer #(.width(16)) multiplexer_1 (
    .in0(bit_extender_1_out), .in1(bit_extender_2_out), .out(multiplexer_1_out), .sel(immselectable));
  Decoder #(.enable("false"), .select(3)) decoder_1 (
    .out1(decoder_1_out1), .out2(decoder_1_out2), .out3(decoder_1_out3), .out4(decoder_1_out4), .sel(regabctl));  // open: out0, out5, out6, out7
  assign bit_extender_2_out = {{12{1'b0}}, IR[4:1]};  // Bit_Extender bit_extender_2
  not not_1 (not_1_out, decoder_2_out2);
  and and_1 (and_1_out, decoder_1_out2, not_1_out);
  or or_1 (or_1_out, and_1_out, decoder_1_out1);
  three_one_AND three_one_and_1 (.in1D(or_1_out), .in3(IR[7:5]), .out3(three_one_and_1_out3));  // open: in1U
  assign RA = three_one_and_1_out3 | three_one_and_2_out3;  // OR_Gate or_2, 3 bits wide
  assign bit_extender_3_out = {{5{1'b0}}, IR[10:0]};  // Bit_Extender bit_extender_3
  three_one_AND three_one_and_2 (.in1D(decoder_1_out3), .in3(IR[10:8]), .out3(three_one_and_2_out3));  // open: in1U
  Multiplexer #(.width(16)) multiplexer_2 (
    .in0(bit_extender_3_out), .in1(bit_extender_4_out), .out(multiplexer_2_out), .sel(immselectable));
  Multiplexer #(.select(2), .width(16)) multiplexer_3 (
    .in1(multiplexer_1_out), .in2(multiplexer_2_out), .in3(multiplexer_4_out), .out(immediate), .sel(immctl));  // open: in0
  not not_2 (not_2_out, decoder_2_out3);
  and and_2 (and_2_out, decoder_1_out1, not_2_out);
  three_one_AND three_one_and_3 (.in1D(and_2_out), .in3(IR[4:2]), .out3(RB));  // open: in1U
  assign bit_extender_4_out = {{6{1'b0}}, IR[10:1]};  // Bit_Extender bit_extender_4
  or or_3 (RA_en, decoder_1_out1, decoder_1_out2, decoder_1_out3);
  not not_3 (not_3_out, decoder_2_out1);
  and and_3 (RB_en, decoder_1_out1, not_3_out);
  assign bit_extender_5_out = {{8{1'b0}}, IR[7:0]};  // Bit_Extender bit_extender_5
  Multiplexer #(.width(16)) multiplexer_4 (
    .in0(bit_extender_5_out), .in1(bit_extender_6_out), .out(multiplexer_4_out), .sel(immselectable));
  assign bit_extender_6_out = {{9{1'b0}}, IR[7:1]};  // Bit_Extender bit_extender_6
  and and_4 (and_4_out, IR[0], immselectable);
  not not_4 (not_4_out, immselectable);
  or or_4 (or_4_out, and_4_out, not_4_out);
  Decoder #(.select(2)) decoder_2 (
    .out1(decoder_2_out1), .out2(decoder_2_out2), .out3(decoder_2_out3), .sel(immctl), .en(or_4_out));  // open: out0
  three_one_AND three_one_and_4 (.in1U(decoder_1_out4), .in3(IR[10:8]), .out3(three_one_and_4_out3));  // open: in1D
  assign flags_direct = {{13{1'b0}}, three_one_and_4_out3};  // Bit_Extender bit_extender_7
  Decoder #(.enable("false"), .select(2)) decoder_3 (
    .out0(decoder_3_out0), .out1(decoder_3_out1), .out2(decoder_3_out2), .out3(decoder_3_out3), .sel(regwctl));
  three_one_AND three_one_and_5 (.in1U(decoder_3_out3), .in3(3'b110), .out3(three_one_and_5_out3));  // open: in1D
  three_one_AND three_one_and_6 (.in1U(decoder_3_out2), .in3(3'b111), .out3(three_one_and_6_out3));  // open: in1D
  three_one_AND three_one_and_7 (.in1U(decoder_3_out1), .in3(IR[10:8]), .out3(three_one_and_7_out3));  // open: in1D
  assign RW = three_one_and_5_out3 | three_one_and_6_out3 | three_one_and_7_out3;  // OR_Gate or_5, 3 bits wide
  not not_5 (W_en, decoder_3_out0);

  assign Opcode = {IR[11], IR[12], IR[13], IR[14], IR[15]};

  // Notes on the sheet:
  //   Op1
  //   Opcode /5
  //   Low Word /11
  //   Op2
  //   Op3
  //   imm5
  //   imm4
  //   imm11
  //   imm8
  //   imm10
  //   imm7
  //   Immediates are controlled by immctl and immen
  //   ImmEn
  //   If immen is set high, immediates lose their lowest SB to become the immediate enable bit
  //   (r6 LINK)
  //   (r7)
endmodule

module CU_decoder (
  input  [35:0] CONTROL_WORD_IN,
  output [1:0] seqsctl,
  output pc_in,
  output fetch,
  output [2:0] addrbusctl,
  output pcouta,
  output [2:0] regoutctl,
  output [1:0] regwctl,
  output imm_enable,
  output [1:0] imm_ctl,
  output alu_latch_a,
  output alu_latch_b,
  output [3:0] alu_select,
  output [1:0] alu_writectl,
  output alu_eflags_en,
  output dbus_b,
  output dbus_rw,
  output dbus_in_w,
  output mar_in,
  output mdr_in
);


  assign addrbusctl = CONTROL_WORD_IN[6:4];
  assign alu_eflags_en = CONTROL_WORD_IN[26];
  assign alu_latch_a = CONTROL_WORD_IN[18];
  assign alu_latch_b = CONTROL_WORD_IN[19];
  assign alu_select = CONTROL_WORD_IN[23:20];
  assign alu_writectl = CONTROL_WORD_IN[25:24];
  assign dbus_b = CONTROL_WORD_IN[29];
  assign dbus_in_w = CONTROL_WORD_IN[31];
  assign dbus_rw = CONTROL_WORD_IN[30];
  assign fetch = CONTROL_WORD_IN[3];
  assign imm_ctl = CONTROL_WORD_IN[16:15];
  assign imm_enable = CONTROL_WORD_IN[14];
  assign mar_in = CONTROL_WORD_IN[32];
  assign mdr_in = CONTROL_WORD_IN[33];
  assign pc_in = CONTROL_WORD_IN[2];
  assign pcouta = CONTROL_WORD_IN[7];
  assign regoutctl = CONTROL_WORD_IN[10:8];
  assign regwctl = CONTROL_WORD_IN[12:11];
  assign seqsctl = CONTROL_WORD_IN[1:0];

  // Notes on the sheet:
  //   CONTROL
  //   REGISTERS
  //   ALU
  //   MEMORY
  //   Reserved
  //   Reserved
endmodule

module sixteen_one_AND (
  input  in1U,
  input  in1D,
  input  [15:0] in16,
  output [15:0] out16
);

  wire xor_1_out;

  xor xor_1 (xor_1_out, in1U, in1D);
  assign out16[1] = xor_1_out ? in16[1] : 1'bz;  // Controlled_Buffer controlled_buffer_1
  assign out16[3] = xor_1_out ? in16[3] : 1'bz;  // Controlled_Buffer controlled_buffer_2
  assign out16[5] = xor_1_out ? in16[5] : 1'bz;  // Controlled_Buffer controlled_buffer_3
  assign out16[7] = xor_1_out ? in16[7] : 1'bz;  // Controlled_Buffer controlled_buffer_4
  assign out16[9] = xor_1_out ? in16[9] : 1'bz;  // Controlled_Buffer controlled_buffer_5
  assign out16[11] = xor_1_out ? in16[11] : 1'bz;  // Controlled_Buffer controlled_buffer_6
  assign out16[13] = xor_1_out ? in16[13] : 1'bz;  // Controlled_Buffer controlled_buffer_7
  assign out16[15] = xor_1_out ? in16[15] : 1'bz;  // Controlled_Buffer controlled_buffer_8
  assign out16[0] = xor_1_out ? in16[0] : 1'bz;  // Controlled_Buffer controlled_buffer_9
  assign out16[2] = xor_1_out ? in16[2] : 1'bz;  // Controlled_Buffer controlled_buffer_10
  assign out16[4] = xor_1_out ? in16[4] : 1'bz;  // Controlled_Buffer controlled_buffer_11
  assign out16[6] = xor_1_out ? in16[6] : 1'bz;  // Controlled_Buffer controlled_buffer_12
  assign out16[8] = xor_1_out ? in16[8] : 1'bz;  // Controlled_Buffer controlled_buffer_13
  assign out16[10] = xor_1_out ? in16[10] : 1'bz;  // Controlled_Buffer controlled_buffer_14
  assign out16[12] = xor_1_out ? in16[12] : 1'bz;  // Controlled_Buffer controlled_buffer_15
  assign out16[14] = xor_1_out ? in16[14] : 1'bz;  // Controlled_Buffer controlled_buffer_16
endmodule

module three_one_AND (
  input  in1U,
  input  in1D,
  input  [2:0] in3,
  output [2:0] out3
);

  wire or_1_out;

  or or_1 (or_1_out, in1U, in1D);
  and and_1 (out3[0], or_1_out, in3[0]);
  and and_2 (out3[1], or_1_out, in3[1]);
  and and_3 (out3[2], or_1_out, in3[2]);
endmodule

module ZeroFlag (
  input  in1,
  input  [15:0] in16,
  output zero,
  output neg,
  output pos
);

  wire and_1_out, and_2_out, and_3_out, and_4_out, and_5_out, and_6_out, and_7_out, and_8_out, and_9_out,
       and_10_out, and_11_out, and_12_out, and_13_out, and_14_out, and_15_out, or_1_out;

  and and_1 (and_1_out, in1, in16[0]);
  and and_2 (and_2_out, in1, in16[1]);
  and and_3 (and_3_out, in1, in16[2]);
  and and_4 (and_4_out, in1, in16[3]);
  and and_5 (and_5_out, in1, in16[4]);
  and and_6 (and_6_out, in1, in16[5]);
  and and_7 (and_7_out, in1, in16[6]);
  and and_8 (and_8_out, in1, in16[7]);
  and and_9 (and_9_out, in1, in16[8]);
  and and_10 (and_10_out, in1, in16[9]);
  and and_11 (and_11_out, in1, in16[10]);
  and and_12 (and_12_out, in1, in16[11]);
  and and_13 (and_13_out, in1, in16[12]);
  and and_14 (and_14_out, in1, in16[13]);
  and and_15 (and_15_out, in1, in16[14]);
  and and_16 (neg, in1, in16[15]);
  or or_1 (or_1_out, and_1_out, and_2_out, and_3_out, and_4_out, and_5_out, and_6_out, and_7_out, and_8_out, and_9_out, and_10_out, and_11_out, and_12_out, and_13_out, and_14_out, and_15_out, neg);
  not not_1 (pos, neg);
  not not_2 (zero, or_1_out);
endmodule

module CU_REG_DECODER (
  input  [1:0] regsel,
  input  [2:0] op1,
  input  [2:0] op2,
  input  [2:0] op3,
  output [2:0] A,
  output [2:0] B,
  output [2:0] W,
  output regen,
  output [15:0] A_bus
);

  wire and_1_out, decoder_1_out0, decoder_1_out1, decoder_1_out2, decoder_1_out3, not_1_out, not_2_out,
       or_1_out, or_3_out;
  wire [2:0] three_one_and_5_out3, three_one_and_6_out3;

  Decoder #(.enable("false"), .select(2)) decoder_1 (
    .out0(decoder_1_out0), .out1(decoder_1_out1), .out2(decoder_1_out2), .out3(decoder_1_out3), .sel(regsel));
  or or_1 (or_1_out, decoder_1_out0, decoder_1_out2);
  and and_1 (and_1_out, not_1_out, not_2_out);
  three_one_AND three_one_and_1 (.in1D(or_1_out), .in3(op1), .out3(A));  // open: in1U
  three_one_AND three_one_and_2 (.in1U(and_1_out), .in3(op3), .out3(A));  // open: in1D
  not not_1 (not_1_out, or_1_out);
  not not_2 (not_2_out, decoder_1_out3);
  or or_2 (regen, and_1_out, or_3_out);
  or or_3 (or_3_out, decoder_1_out0, decoder_1_out1);
  three_one_AND three_one_and_3 (.in1D(or_3_out), .in3(op2), .out3(B));  // open: in1U
  three_one_AND three_one_and_4 (.in1D(not_2_out), .in3(op1), .out3(W));  // open: in1U
  three_one_AND three_one_and_5 (.in1U(decoder_1_out3), .in3(op2), .out3(three_one_and_5_out3));  // open: in1D
  three_one_AND three_one_and_6 (.in1U(decoder_1_out3), .in3(op1), .out3(three_one_and_6_out3));  // open: in1D
  assign A_bus = {{10{1'b0}}, {three_one_and_5_out3, three_one_and_6_out3}};  // Bit_Extender bit_extender_1
endmodule

module test1 (
  input  [15:0] in_1,
  input  [15:0] imm,
  input  in_3
);

  wire clock_1_out, nor_1_out, not_1_out;
  wire [15:0] or_1_out, register_1_q, sixteen_one_and_1_out16, sixteen_one_and_2_out16;

  Clock #(.lowDuration(4), .phaseOffset(3)) clock_1 (.out(clock_1_out));
  not not_1 (not_1_out, clock_1_out);
  sixteen_one_AND sixteen_one_and_1 (.in1U(not_1_out), .in16(imm), .out16(sixteen_one_and_1_out16));  // open: in1D
  sixteen_one_AND sixteen_one_and_2 (.in1D(clock_1_out), .in16(in_1), .out16(sixteen_one_and_2_out16));  // open: in1U
  assign or_1_out = sixteen_one_and_2_out16 | sixteen_one_and_1_out16;  // OR_Gate or_1, 16 bits wide
  nor nor_1 (nor_1_out, not_1_out, clock_1_out);
  // Probe on or_1_out
  Register #(.trigger("falling"), .width(16)) register_1 (
    .D(or_1_out), .en(in_3), .clk(nor_1_out), .Q(register_1_q));  // open: clr
  LedBar #(.matrixcols(16)) ledbar_1 (
    .led0(register_1_q[15]), .led1(register_1_q[14]), .led2(register_1_q[13]), .led3(register_1_q[12]),
    .led4(register_1_q[11]), .led5(register_1_q[10]), .led6(register_1_q[9]), .led7(register_1_q[8]),
    .led8(register_1_q[7]), .led9(register_1_q[6]), .led10(register_1_q[5]), .led11(register_1_q[4]),
    .led12(register_1_q[3]), .led13(register_1_q[2]), .led14(register_1_q[1]), .led15(register_1_q[0]));
endmodule

module CU_FETCH (
  input  pc_write,
  input  pc_in,
  input  pc_fetch
);

  wire [15:0] and_1_p2, and_1_p3, or_1_out;
  wire [15:1] undriven;

  assign or_1_out = {undriven, pc_in} | and_1_p2;  // OR_Gate or_1, 16 bits wide
  // AND_Gate and_1: pin names not known; wires that end beside it: pc_fetch, and_1_p2, and_1_p3
  Register #(.width(16)) PC (.D(or_1_out), .en(pc_write), .Q(and_1_p3));  // open: clk, clr
  // Pins of 1 and 16 bits meet at {undriven, pc_in}
endmodule

module CU_REG_DECD2 (
  input  [1:0] r1sel,
  input  [1:0] r2sel,
  input  [1:0] rwsel,
  input  [2:0] op1,
  input  [2:0] op2,
  input  [2:0] op3,
  output [2:0] r1,
  output [2:0] r2,
  output [2:0] rw
);

  Multiplexer #(.select(2), .width(3)) multiplexer_1 (
    .in1(op3), .in2(op2), .in3(op1), .out(r1), .sel(r1sel));  // open: in0
  Multiplexer #(.select(2), .width(3)) multiplexer_2 (
    .in1(op3), .in2(op2), .in3(op1), .out(r2), .sel(r2sel));  // open: in0
  Multiplexer #(.select(2), .width(3)) multiplexer_3 (
    .in1(op3), .in2(op2), .in3(op1), .out(rw), .sel(rwsel));  // open: in0
endmodule

module CU_DECODER2 (
  input  [35:0] CONTROL_WORD_IN,
  output [1:0] seqsctl,
  output addrbus_pc_in,
  output fetch,
  output [1:0] addrbus_out_sel,
  output [1:0] r1ctl,
  output [1:0] r2ctl,
  output [1:0] rwctl,
  output [1:0] abusctl,
  output [1:0] bbusctl,
  output imm_enable,
  output [1:0] imm_ctl,
  output alu_latch_a,
  output alu_latch_b,
  output [3:0] alu_select,
  output [1:0] alu_writectl,
  output alu_eflags_en,
  output mem_b_in,
  output mem_b_out
);


  assign abusctl = CONTROL_WORD_IN[15:14];
  assign addrbus_out_sel = CONTROL_WORD_IN[5:4];
  assign addrbus_pc_in = CONTROL_WORD_IN[2];
  assign alu_eflags_en = CONTROL_WORD_IN[30];
  assign alu_latch_a = CONTROL_WORD_IN[22];
  assign alu_latch_b = CONTROL_WORD_IN[23];
  assign alu_select = CONTROL_WORD_IN[27:24];
  assign alu_writectl = CONTROL_WORD_IN[29:28];
  assign bbusctl = CONTROL_WORD_IN[17:16];
  assign fetch = CONTROL_WORD_IN[3];
  assign imm_ctl = CONTROL_WORD_IN[20:19];
  assign imm_enable = CONTROL_WORD_IN[18];
  assign mem_b_in = CONTROL_WORD_IN[33];
  assign mem_b_out = CONTROL_WORD_IN[34];
  assign r1ctl = CONTROL_WORD_IN[9:8];
  assign r2ctl = CONTROL_WORD_IN[11:10];
  assign rwctl = CONTROL_WORD_IN[13:12];
  assign seqsctl = CONTROL_WORD_IN[1:0];

  // Notes on the sheet:
  //   CONTROL
  //   REGISTERS
  //   ALU
  //   MEMORY
  //   Reserved
  //   Reserved
  //   Reserved for control
endmodule

module CU_regdecoder3 (
  input  [2:0] abbusctl,
  input  [2:0] wbusctl,
  input  [2:0] op1,
  input  [2:0] op2,
  input  [2:0] op3,
  input  [2:0] rip,
  output [2:0] A,
  output [2:0] B,
  output [2:0] W
);

  wire decoder_1_out1, decoder_1_out2, decoder_1_out3, decoder_1_out4, or_1_out, or_2_out, or_5_out, or_6_out;
  wire [2:0] three_one_and_1_out3, three_one_and_2_out3, three_one_and_3_out3, three_one_and_4_out3,
       three_one_and_5_out3, three_one_and_6_out3;

  Decoder #(.enable("false"), .select(3)) decoder_1 (
    .out1(decoder_1_out1), .out2(decoder_1_out2), .out3(decoder_1_out3), .out4(decoder_1_out4), .sel(abbusctl));  // open: out0, out5, out6, out7
  or or_1 (or_1_out, decoder_1_out1, decoder_1_out2);
  three_one_AND three_one_and_1 (.in1D(or_1_out), .in3(op2), .out3(three_one_and_1_out3));  // open: in1U
  or or_2 (or_2_out, decoder_1_out3, decoder_1_out4);
  three_one_AND three_one_and_2 (.in1D(or_2_out), .in3(rip), .out3(three_one_and_2_out3));  // open: in1U
  assign A = three_one_and_1_out3 | three_one_and_2_out3;  // OR_Gate or_3, 3 bits wide
  three_one_AND three_one_and_3 (.in1D(decoder_1_out2), .in3(op3), .out3(three_one_and_3_out3));  // open: in1U
  three_one_AND three_one_and_4 (.in1D(decoder_1_out3), .in3(op1), .out3(three_one_and_4_out3));  // open: in1U
  assign B = three_one_and_3_out3 | three_one_and_4_out3;  // OR_Gate or_4, 3 bits wide
  or or_5 (or_5_out, decoder_1_out1, decoder_1_out2);
  or or_6 (or_6_out, decoder_1_out3, decoder_1_out4);
  three_one_AND three_one_and_5 (.in1D(or_5_out), .in3(op1), .out3(three_one_and_5_out3));  // open: in1U
  three_one_AND three_one_and_6 (.in1D(or_6_out), .in3(rip), .out3(three_one_and_6_out3));  // open: in1U
  assign W = three_one_and_5_out3 | three_one_and_6_out3;  // OR_Gate or_7, 3 bits wide
  Decoder #(.enable("false"), .select(3)) decoder_2 (.sel(wbusctl));  // open: out0, out1, out2, out3, out4, out5, out6, out7
endmodule

module CU_regdecoder4 (
  input  [2:0] readctl,
  input  [1:0] regwctl,
  input  [2:0] op1,
  input  [2:0] op2,
  input  [2:0] op3,
  input  immen,
  output W_en,
  output [2:0] RB,
  output [15:0] flags_direct,
  output RA_en,
  output RB_en,
  output [2:0] RW,
  output [2:0] RA
);

  wire and_1_out, decoder_1_out2, decoder_1_out3, decoder_1_out4, decoder_2_out0, decoder_2_out1,
       decoder_2_out2, decoder_2_out3, not_1_out, or_1_out;
  wire [2:0] three_one_and_1_out3, three_one_and_2_out3, three_one_and_4_out3, three_one_and_5_out3,
       three_one_and_6_out3, three_one_and_7_out3;

  not not_1 (not_1_out, immen);
  Decoder #(.enable("false"), .select(3)) decoder_1 (
    .out1(RB_en), .out2(decoder_1_out2), .out3(decoder_1_out3), .out4(decoder_1_out4), .sel(readctl));  // open: out0, out5, out6, out7
  or or_1 (or_1_out, RB_en, decoder_1_out2);
  three_one_AND three_one_and_1 (.in1D(or_1_out), .in3(op2), .out3(three_one_and_1_out3));  // open: in1U
  three_one_AND three_one_and_2 (.in1D(decoder_1_out3), .in3(op1), .out3(three_one_and_2_out3));  // open: in1U
  assign RA = three_one_and_1_out3 | three_one_and_2_out3;  // OR_Gate or_2, 3 bits wide
  and and_1 (and_1_out, RB_en, not_1_out);
  three_one_AND three_one_and_3 (.in1D(and_1_out), .in3(op3), .out3(RB));  // open: in1U
  or or_3 (RA_en, RB_en, decoder_1_out2, decoder_1_out3);
  three_one_AND three_one_and_4 (.in1U(decoder_1_out4), .in3(op1), .out3(three_one_and_4_out3));  // open: in1D
  assign flags_direct = {{13{1'b0}}, three_one_and_4_out3};  // Bit_Extender bit_extender_1
  Decoder #(.enable("false"), .select(2)) decoder_2 (
    .out0(decoder_2_out0), .out1(decoder_2_out1), .out2(decoder_2_out2), .out3(decoder_2_out3), .sel(regwctl));
  three_one_AND three_one_and_5 (.in1U(decoder_2_out3), .in3(3'b110), .out3(three_one_and_5_out3));  // open: in1D
  three_one_AND three_one_and_6 (.in1U(decoder_2_out2), .in3(3'b111), .out3(three_one_and_6_out3));  // open: in1D
  assign RW = three_one_and_5_out3 | three_one_and_6_out3 | three_one_and_7_out3;  // OR_Gate or_4, 3 bits wide
  three_one_AND three_one_and_7 (.in1U(decoder_2_out1), .in3(op1), .out3(three_one_and_7_out3));  // open: in1D
  not not_2 (W_en, decoder_2_out0);

  // Notes on the sheet:
  //   (r6 LINK)
  //   (r7)
endmodule

module CPU (
  input  [15:0] dbus_in,
  output CLK_out,
  output dbus_rw,
  output [15:0] addrbus_out,
  output [15:0] dbus_out
);

  wire and_1_out, and_2_out, cascadingandx16_1_out1, cu_decoder_1_alu_eflags_en, cu_decoder_1_alu_latch_a,
       cu_decoder_1_alu_latch_b, cu_decoder_1_dbus_b, cu_decoder_1_dbus_in_w, cu_decoder_1_fetch,
       cu_decoder_1_imm_enable, cu_decoder_1_mar_in, cu_decoder_1_mdr_in, cu_decoder_1_pc_in,
       cu_decoder_1_pcouta, cu_instructiondecoder_1_ra_en, cu_instructiondecoder_1_rb_en,
       cu_instructiondecoder_1_w_en, decoder_1_out1, decoder_1_out2, decoder_1_out3, decoder_1_out4,
       decoder_1_out5, decoder_2_out0, decoder_2_out2, end_execution_out, instruction_FSM_s2,
       instruction_FSM_s4, not_1_out, not_2_out, not_4_out, not_5_out, not_6_out, not_7_out, or_1_out,
       or_2_out, pause_out, reset_out;
  wire [1:0] cu_decoder_1_alu_writectl, cu_decoder_1_imm_ctl, cu_decoder_1_regwctl, cu_decoder_1_seqsctl,
       execution_FSM_fsm_out;
  wire [2:0] cu_decoder_1_addrbusctl, cu_decoder_1_regoutctl, cu_instructiondecoder_1_ra,
       cu_instructiondecoder_1_rb, cu_instructiondecoder_1_rw;
  wire [3:0] cu_decoder_1_alu_select;
  wire [6:2] cu_instructiondecoder_1_opcode;
  wire [15:0] adder_1_out, alu_1_alu_out, alu_1_eflags_out, controlled_buffer_2_out,
       cu_instructiondecoder_1_immediate, IR_q, MAR_o, MDR_q, not_3_out, PC_q, pre_IR_o,
       sixteen_one_and_1_out16, sixteen_one_and_2_out16, sixteen_one_and_4_out16, sixteen_one_and_12_out16,
       sixteen_one_and_13_out16, sixteen_one_and_14_out16;
  wire [35:0] pla_1_out;

  Clock clock_1 (.out(CLK_out));
  FourFSM execution_FSM (
    .clk(CLK_out), .pause(pause_out), .rst(reset_out), .fsm_out(execution_FSM_fsm_out));  // open: s1, s2, s3, s4
  and reset (reset_out, end_execution_out, instruction_FSM_s4);
  and pause (pause_out, end_execution_out, not_1_out);
  not not_1 (not_1_out, instruction_FSM_s4);
  Register #(.width(16)) IR (.D(pre_IR_o), .en(instruction_FSM_s4), .clk(CLK_out), .Q(IR_q));  // open: clr
  FourFSM instruction_FSM (
    .clk(CLK_out), .pause(not_2_out), .s2(instruction_FSM_s2), .s4(instruction_FSM_s4));  // open: rst, fsm_out, s1, s3
  not not_2 (not_2_out, cu_decoder_1_fetch);
  or end_execution (end_execution_out, decoder_2_out0, cascadingandx16_1_out1);
  GPREG_3 pre_IR (.D(sixteen_one_and_1_out16), .WRITE_ENABLE(instruction_FSM_s2), .ENABLE(CLK_out), .O(pre_IR_o));
  sixteen_one_AND sixteen_one_and_1 (
    .in1D(instruction_FSM_s2), .in16(dbus_in), .out16(sixteen_one_and_1_out16));  // open: in1U
  Register #(.width(16)) PC (.D(sixteen_one_and_4_out16), .en(or_1_out), .clk(CLK_out), .Q(PC_q));  // open: clr
  or or_1 (or_1_out, cu_decoder_1_pc_in, instruction_FSM_s2);
  // Probe on pre_IR_o
  // Probe on sixteen_one_and_1_out16
  cascadingANDx16 cascadingandx16_1 (.in1(decoder_2_out2), .in16(not_3_out), .out1(cascadingandx16_1_out1));
  Decoder #(.enable("false"), .select(3)) decoder_1 (
    .out1(decoder_1_out1), .out2(decoder_1_out2), .out3(decoder_1_out3), .out4(decoder_1_out4),
    .out5(decoder_1_out5), .sel(cu_decoder_1_addrbusctl));  // open: out0, out6, out7
  sixteen_one_AND sixteen_one_and_2 (
    .in1U(cu_decoder_1_pcouta), .in16(PC_q), .out16(sixteen_one_and_2_out16));  // open: in1D
  Adder #(.width(16)) adder_1 (.a(PC_q), .b(16'h1), .out(adder_1_out));  // open: cin, cout
  sixteen_one_AND sixteen_one_and_3 (.in1U(decoder_1_out5), .in16(16'h100), .out16(adder_1_out));  // open: in1D
  assign not_3_out = ~sixteen_one_and_12_out16;  // NOT_Gate not_3, 16 bits wide
  sixteen_one_AND sixteen_one_and_4 (
    .in1U(decoder_1_out3), .in16(PC_q), .out16(sixteen_one_and_4_out16));  // open: in1D
  or or_2 (or_2_out, decoder_1_out4, instruction_FSM_s2);
  // Probe on adder_1_out
  sixteen_one_AND sixteen_one_and_5 (.in1D(instruction_FSM_s2), .in16(PC_q), .out16(addrbus_out));  // open: in1U
  // Probe on addrbus_out
  // Probe on pla_1_out
  PLA #(.in_width(7), .out_width(36), .\table ("0000000 000000000000000000000000000000001000\n1000000 000000000001001111001100100100001000\n1000100 000000000001010011001100100100001000\n1001000 000000000001010111001100100100001000\n1001100 000000000001000011001100100100001000\n1010000 000000000001000111001100100100001000\n1010100 000000000001000111001100100100001000\n0011000 000000000001011011001100100100001000\n1011100 000000000001011111001100100100001000\n1100000 000000000001011111001100100100001000\n0100000 000000000001001111011100101000001000\n0100100 001100000001001111011100001000100001\n0100101 000000100001001110000000100000001000")) pla_1 (
    .in({cu_instructiondecoder_1_opcode, execution_FSM_fsm_out}), .out(pla_1_out));
  // Probe on sixteen_one_and_4_out16
  sixteen_one_AND sixteen_one_and_6 (
    .in1U(or_2_out), .in16(adder_1_out), .out16(sixteen_one_and_4_out16));  // open: in1D
  // Probe on sixteen_one_and_4_out16
  not not_4 (not_4_out, instruction_FSM_s2);
  sixteen_one_AND sixteen_one_and_7 (
    .in1U(not_4_out), .in16(sixteen_one_and_4_out16), .out16(addrbus_out));  // open: in1D
  // Probe on addrbus_out
  Decoder #(.enable("false"), .select(2)) decoder_2 (
    .out0(decoder_2_out0), .out2(decoder_2_out2), .sel(cu_decoder_1_seqsctl));  // open: out1, out3
  assign sixteen_one_and_4_out16 = decoder_1_out2 ? sixteen_one_and_12_out16 : 16'bz;  // Controlled_Buffer controlled_buffer_1
  sixteen_one_AND sixteen_one_and_8 (
    .in1U(decoder_1_out1), .in16(MAR_o), .out16(sixteen_one_and_4_out16));  // open: in1D
  GPREG_3 MAR (.D(sixteen_one_and_4_out16), .WRITE_ENABLE(cu_decoder_1_mar_in), .ENABLE(CLK_out), .O(MAR_o));
  Register #(.trigger("falling"), .width(16)) MDR (
    .D(controlled_buffer_2_out), .en(cu_decoder_1_mdr_in), .clk(CLK_out), .Q(MDR_q));  // open: clr
  CU_instructiondecoder cu_instructiondecoder_1 (
    .immctl(cu_decoder_1_imm_ctl), .immselectable(cu_decoder_1_imm_enable), .regwctl(cu_decoder_1_regwctl),
    .IR(IR_q), .regabctl(cu_decoder_1_regoutctl), .RB(cu_instructiondecoder_1_rb),
    .RA_en(cu_instructiondecoder_1_ra_en), .RB_en(cu_instructiondecoder_1_rb_en),
    .flags_direct(sixteen_one_and_2_out16), .RW(cu_instructiondecoder_1_rw),
    .W_en(cu_instructiondecoder_1_w_en),
    .opcode({cu_instructiondecoder_1_opcode[2], cu_instructiondecoder_1_opcode[3], cu_instructiondecoder_1_opcode[4], cu_instructiondecoder_1_opcode[5], cu_instructiondecoder_1_opcode[6]}),
    .RA(cu_instructiondecoder_1_ra), .immediate(cu_instructiondecoder_1_immediate));
  not not_5 (not_5_out, cu_decoder_1_mdr_in);
  assign controlled_buffer_2_out = not_5_out ? MDR_q : 16'bz;  // Controlled_Buffer controlled_buffer_2
  sixteen_one_AND sixteen_one_and_9 (
    .in1U(cu_decoder_1_dbus_b), .in16(controlled_buffer_2_out), .out16(cu_instructiondecoder_1_immediate));  // open: in1D
  assign controlled_buffer_2_out = cu_decoder_1_mdr_in ? dbus_in : 16'bz;  // Controlled_Buffer controlled_buffer_3
  sixteen_one_AND sixteen_one_and_10 (
    .in1U(cu_decoder_1_dbus_in_w), .in16(sixteen_one_and_12_out16), .out16(dbus_out));  // open: in1D
  // Probe on dbus_out
  CU_decoder cu_decoder_1 (
    .CONTROL_WORD_IN(pla_1_out), .alu_latch_a(cu_decoder_1_alu_latch_a),
    .alu_latch_b(cu_decoder_1_alu_latch_b), .dbus_b(cu_decoder_1_dbus_b), .dbus_rw(dbus_rw),
    .dbus_in_w(cu_decoder_1_dbus_in_w), .mar_in(cu_decoder_1_mar_in), .mdr_in(cu_decoder_1_mdr_in),
    .imm_enable(cu_decoder_1_imm_enable), .alu_writectl(cu_decoder_1_alu_writectl),
    .alu_eflags_en(cu_decoder_1_alu_eflags_en), .seqsctl(cu_decoder_1_seqsctl), .pc_in(cu_decoder_1_pc_in),
    .fetch(cu_decoder_1_fetch), .addrbusctl(cu_decoder_1_addrbusctl), .pcouta(cu_decoder_1_pcouta),
    .regoutctl(cu_decoder_1_regoutctl), .regwctl(cu_decoder_1_regwctl), .alu_select(cu_decoder_1_alu_select),
    .imm_ctl(cu_decoder_1_imm_ctl));
  GPREG_BANK gpreg_bank_1 (
    .write_i(sixteen_one_and_12_out16), .write_sel(cu_instructiondecoder_1_rw), .CLK(CLK_out),
    .write_enable(cu_instructiondecoder_1_w_en), .read2_en(cu_instructiondecoder_1_rb_en),
    .read1_en(cu_instructiondecoder_1_ra_en), .read2_sel(cu_instructiondecoder_1_rb),
    .read1_sel(cu_instructiondecoder_1_ra), .read2_o(cu_instructiondecoder_1_immediate),
    .read1_o(sixteen_one_and_2_out16));
  sixteen_one_AND sixteen_one_and_11 (
    .in1D(and_1_out), .in16(alu_1_eflags_out), .out16(cu_instructiondecoder_1_immediate));  // open: in1U
  // Probe on cu_instructiondecoder_1_immediate
  not not_6 (not_6_out, cu_decoder_1_alu_writectl[0]);
  not not_7 (not_7_out, cu_decoder_1_alu_writectl[1]);
  and and_1 (and_1_out, cu_decoder_1_alu_writectl[1], not_6_out);
  and and_2 (and_2_out, not_7_out, cu_decoder_1_alu_writectl[0]);
  sixteen_one_AND sixteen_one_and_12 (
    .in1D(and_2_out), .in16(alu_1_alu_out), .out16(sixteen_one_and_12_out16));  // open: in1U
  // Probe on sixteen_one_and_2_out16
  sixteen_one_AND sixteen_one_and_13 (
    .in1U(cu_decoder_1_alu_latch_b), .in16(cu_instructiondecoder_1_immediate),
    .out16(sixteen_one_and_13_out16));  // open: in1D
  // Probe on sixteen_one_and_12_out16
  sixteen_one_AND sixteen_one_and_14 (
    .in1U(cu_decoder_1_alu_latch_a), .in16(sixteen_one_and_2_out16), .out16(sixteen_one_and_14_out16));  // open: in1D
  ALU alu_1 (
    .reg_a(sixteen_one_and_14_out16), .reg_b(sixteen_one_and_13_out16), .ALU_select(cu_decoder_1_alu_select),
    .CLK(CLK_out), .EFLAGS_write(cu_decoder_1_alu_eflags_en), .EFLAGS_out(alu_1_eflags_out),
    .alu_out(alu_1_alu_out));

  // Notes on the sheet:
  //   wait until pc is ready & end, else reset
  //   INCREMENTER
  //   addrctl decoder
  //   ADDRBUS
  //   DBUS
  //   W
  //   A
  //   B
  //   EFLAGS
  //   OUT
  //   memory control line
endmodule

module GPREG_4 (
  input  [15:0] D,
  input  WRITE_ENABLE,
  input  ENABLE,
  output [15:0] O
);

  wire and_1_out;

  and and_1 (and_1_out, WRITE_ENABLE, ENABLE);
  D_FF_rising d_ff_rising_1 (.CLK(and_1_out), .D(D[0]), .O(O[0]));  // open: O_inv
  D_FF_rising d_ff_rising_2 (.CLK(and_1_out), .D(D[1]), .O(O[1]));  // open: O_inv
  D_FF_rising d_ff_rising_3 (.CLK(and_1_out), .D(D[2]), .O(O[2]));  // open: O_inv
  D_FF_rising d_ff_rising_4 (.CLK(and_1_out), .D(D[3]), .O(O[3]));  // open: O_inv
  D_FF_rising d_ff_rising_5 (.CLK(and_1_out), .D(D[4]), .O(O[4]));  // open: O_inv
  D_FF_rising d_ff_rising_6 (.CLK(and_1_out), .D(D[5]), .O(O[5]));  // open: O_inv
  D_FF_rising d_ff_rising_7 (.CLK(and_1_out), .D(D[6]), .O(O[6]));  // open: O_inv
  D_FF_rising d_ff_rising_8 (.CLK(and_1_out), .D(D[7]), .O(O[7]));  // open: O_inv
  D_FF_rising d_ff_rising_9 (.CLK(and_1_out), .D(D[8]), .O(O[8]));  // open: O_inv
  D_FF_rising d_ff_rising_10 (.CLK(and_1_out), .D(D[9]), .O(O[9]));  // open: O_inv
  D_FF_rising d_ff_rising_11 (.CLK(and_1_out), .D(D[10]), .O(O[10]));  // open: O_inv
  D_FF_rising d_ff_rising_12 (.CLK(and_1_out), .D(D[11]), .O(O[11]));  // open: O_inv
  D_FF_rising d_ff_rising_13 (.CLK(and_1_out), .D(D[12]), .O(O[12]));  // open: O_inv
  D_FF_rising d_ff_rising_14 (.CLK(and_1_out), .D(D[13]), .O(O[13]));  // open: O_inv
  D_FF_rising d_ff_rising_15 (.CLK(and_1_out), .D(D[14]), .O(O[14]));  // open: O_inv
  D_FF_rising d_ff_rising_16 (.CLK(and_1_out), .D(D[15]), .O(O[15]));  // open: O_inv
endmodule

module lsb16 (
  input  [15:0] i16,
  output o1
);


  assign o1 = i16[0];
endmodule

module FourFSM (
  input  rst,
  input  pause,
  input  clk,
  output s1,
  output s2,
  output s3,
  output s4,
  output [1:0] fsm_out
);

  wire not_1_out, not_2_out, not_3_out, not_4_out, not_5_out, not_6_out, not_7_out, or_1_out, or_2_out;
  wire [1:0] and_1_out;

  not not_1 (not_1_out, fsm_out[1]);
  and s0_0 (s1, not_1_out, not_2_out);
  not not_2 (not_2_out, fsm_out[0]);
  not not_3 (not_3_out, fsm_out[1]);
  and s0_1 (s2, not_3_out, fsm_out[0]);
  and s1_0 (s3, fsm_out[1], not_4_out);
  not not_4 (not_4_out, fsm_out[0]);
  and s1_1 (s4, fsm_out[1], fsm_out[0]);
  Register #(.width(2)) register_1 (.D(and_1_out), .en(not_5_out), .clk(clk), .Q(fsm_out));  // open: clr
  not not_5 (not_5_out, pause);
  or or_1 (or_1_out, s3, s1);
  not not_6 (not_6_out, rst);
  and and_1 (and_1_out[0], or_1_out, not_6_out);
  or or_2 (or_2_out, s3, s2);
  not not_7 (not_7_out, rst);
  and and_2 (and_1_out[1], or_2_out, not_7_out);
endmodule

module IO_controller_2 (
  input  [15:0] p1_in,
  input  [15:0] p2_in,
  input  [15:0] p3_in,
  input  [15:0] p4_in,
  input  WE,
  input  RE,
  input  clk
);

  RAM #(.addrWidth(4), .dataWidth(16)) ram_1 (.we(WE), .oe(RE), .clk(clk));  // open: addr, din, dout
  Priority_Encoder priority_encoder_1 ();  // open: in0, in1, in2, in3, in4, in5, in6, in7, out, en_in, gs, en_out
  Keyboard keyboard_1 ();  // open: clk, re, clr, avail, data

  // Notes on the sheet:
  //   priority encoder as fallback for simultaneous inputs
endmodule

module ExecutionFSM (
  input  fetch_done,
  input  reset_execution
);

  wire not_1_out;

  // AND_Gate reset has open pins: in0=fetch_done, in1=reset_execution, out=open
  not not_1 (not_1_out, fetch_done);
  // AND_Gate pause has open pins: in0=not_1_out, in1=reset_execution, out=open
endmodule

module sixteen_RE_backup (
  input  in1U,
  input  in1D,
  input  [15:0] in16,
  output [15:0] out16
);

  wire xor_1_out;

  xor xor_1 (xor_1_out, in1U, in1D);
  and and_1 (out16[0], xor_1_out, in16[0]);
  and and_2 (out16[1], xor_1_out, in16[1]);
  and and_3 (out16[2], xor_1_out, in16[2]);
  and and_4 (out16[3], xor_1_out, in16[3]);
  and and_5 (out16[4], xor_1_out, in16[4]);
  and and_6 (out16[5], xor_1_out, in16[5]);
  and and_7 (out16[6], xor_1_out, in16[6]);
  and and_8 (out16[7], xor_1_out, in16[7]);
  and and_9 (out16[8], xor_1_out, in16[8]);
  and and_10 (out16[9], xor_1_out, in16[9]);
  and and_11 (out16[10], xor_1_out, in16[10]);
  and and_12 (out16[11], xor_1_out, in16[11]);
  and and_13 (out16[12], xor_1_out, in16[12]);
  and and_14 (out16[13], xor_1_out, in16[13]);
  and and_15 (out16[14], xor_1_out, in16[14]);
  and and_16 (out16[15], xor_1_out, in16[15]);
endmodule

module cascadingANDx16 (
  input  in1,
  input  [15:0] in16,
  output out1
);

  wire and_1_out, and_2_out, and_3_out, and_4_out, and_5_out, and_6_out, and_7_out, and_8_out, and_9_out,
       and_10_out, and_11_out, and_12_out, and_13_out, and_14_out, and_15_out, and_16_out;

  and and_1 (and_1_out, in1, in16[0]);
  and and_2 (and_2_out, in1, in16[1]);
  and and_3 (and_3_out, in1, in16[2]);
  and and_4 (and_4_out, in1, in16[3]);
  and and_5 (and_5_out, in1, in16[4]);
  and and_6 (and_6_out, in1, in16[5]);
  and and_7 (and_7_out, in1, in16[6]);
  and and_8 (and_8_out, in1, in16[7]);
  and and_9 (and_9_out, in1, in16[8]);
  and and_10 (and_10_out, in1, in16[9]);
  and and_11 (and_11_out, in1, in16[10]);
  and and_12 (and_12_out, in1, in16[11]);
  and and_13 (and_13_out, in1, in16[12]);
  and and_14 (and_14_out, in1, in16[13]);
  and and_15 (and_15_out, in1, in16[14]);
  and and_16 (and_16_out, in1, in16[15]);
  or or_1 (out1, and_1_out, and_2_out, and_3_out, and_4_out, and_5_out, and_6_out, and_7_out, and_8_out, and_9_out, and_10_out, and_11_out, and_12_out, and_13_out, and_14_out, and_15_out, and_16_out);
endmodule

module CU_instructiondecoder (
  input  [15:0] IR,
  input  immselectable,
  input  [1:0] immctl,
  input  [2:0] regabctl,
  input  [1:0] regwctl,
  output [4:0] opcode,
  output [15:0] immediate,
  output W_en,
  output [2:0] RA,
  output [2:0] RB,
  output RA_en,
  output RB_en,
  output [2:0] RW,
  output [15:0] flags_direct
);

  wire and_1_out, and_2_out, and_3_out, and_4_out, and_5_out, decoder_1_out1, decoder_1_out2, decoder_1_out3,
       decoder_1_out4, decoder_2_out0, decoder_2_out1, decoder_2_out2, decoder_2_out3, decoder_3_out0,
       decoder_3_out1, decoder_3_out2, decoder_3_out3, not_1_out, not_2_out, not_3_out, not_4_out, not_5_out,
       or_1_out, or_6_out;
  wire [2:0] three_one_and_1_out3, three_one_and_2_out3, three_one_and_3_out3, three_one_and_4_out3,
       three_one_and_5_out3, three_one_and_6_out3, three_one_and_7_out3;
  wire [15:0] bit_extender_1_out, bit_extender_2_out, bit_extender_3_out, bit_extender_4_out,
       bit_extender_5_out, bit_extender_6_out, bit_extender_7_out, multiplexer_1_out, multiplexer_2_out,
       multiplexer_3_out, multiplexer_4_out;

  assign bit_extender_1_out = {{11{IR[4]}}, IR[4:0]};  // Bit_Extender bit_extender_1
  Multiplexer #(.width(16)) multiplexer_1 (
    .in0(bit_extender_1_out), .in1(bit_extender_2_out), .out(multiplexer_1_out), .sel(immselectable));
  Decoder #(.enable("false"), .select(3)) decoder_1 (
    .out1(decoder_1_out1), .out2(decoder_1_out2), .out3(decoder_1_out3), .out4(decoder_1_out4), .sel(regabctl));  // open: out0, out5, out6, out7
  assign bit_extender_2_out = {{12{IR[4]}}, IR[4:1]};  // Bit_Extender bit_extender_2
  buf or_1 (or_1_out, decoder_1_out1);  // OR_Gate
  three_one_AND three_one_and_1 (.in1D(or_1_out), .in3(IR[7:5]), .out3(three_one_and_1_out3));  // open: in1U
  assign RA = three_one_and_1_out3;  // OR_Gate or_2, 3 bits wide OR_Gate
  assign bit_extender_3_out = {{5{IR[10]}}, IR[10:0]};  // Bit_Extender bit_extender_3
  three_one_AND three_one_and_2 (.in1D(decoder_1_out1), .in3(IR[4:2]), .out3(three_one_and_2_out3));  // open: in1U
  Multiplexer #(.width(16)) multiplexer_2 (
    .in0(bit_extender_3_out), .in1(bit_extender_4_out), .out(multiplexer_2_out), .sel(immselectable));
  Multiplexer #(.select(2), .width(16)) multiplexer_3 (
    .in0({16{1'b0}}), .in1(multiplexer_1_out), .in2(multiplexer_2_out), .in3(multiplexer_4_out),
    .out(multiplexer_3_out), .sel(immctl));
  and and_1 (and_1_out, or_6_out, not_1_out);
  assign immediate = and_1_out ? multiplexer_3_out : 16'bz;  // Controlled_Buffer controlled_buffer_1
  three_one_AND three_one_and_3 (.in1D(decoder_1_out2), .in3(IR[7:5]), .out3(three_one_and_3_out3));  // open: in1U
  assign RB = three_one_and_2_out3 | three_one_and_3_out3 | three_one_and_4_out3;  // OR_Gate or_3, 3 bits wide
  assign bit_extender_4_out = {{6{IR[10]}}, IR[10:1]};  // Bit_Extender bit_extender_4
  not not_1 (not_1_out, decoder_2_out0);
  three_one_AND three_one_and_4 (.in1D(decoder_1_out3), .in3(IR[10:8]), .out3(three_one_and_4_out3));  // open: in1U
  buf or_4 (RA_en, decoder_1_out1);  // OR_Gate
  not not_2 (not_2_out, decoder_2_out2);
  and and_2 (and_2_out, decoder_1_out3, not_2_out);
  assign bit_extender_5_out = {{8{IR[7]}}, IR[7:0]};  // Bit_Extender bit_extender_5
  Multiplexer #(.width(16)) multiplexer_4 (
    .in0(bit_extender_5_out), .in1(bit_extender_6_out), .out(multiplexer_4_out), .sel(immselectable));
  not not_3 (not_3_out, decoder_2_out3);
  not not_4 (not_4_out, decoder_2_out1);
  and and_3 (and_3_out, decoder_1_out2, not_3_out);
  and and_4 (and_4_out, decoder_1_out1, not_4_out);
  or or_5 (RB_en, and_2_out, and_3_out, and_4_out);
  assign bit_extender_6_out = {{9{IR[7]}}, IR[7:1]};  // Bit_Extender bit_extender_6
  and and_5 (and_5_out, IR[0], immselectable);
  not not_5 (not_5_out, immselectable);
  or or_6 (or_6_out, and_5_out, not_5_out);
  Decoder #(.select(2)) decoder_2 (
    .out0(decoder_2_out0), .out1(decoder_2_out1), .out2(decoder_2_out2), .out3(decoder_2_out3), .sel(immctl),
    .en(or_6_out));
  assign bit_extender_7_out = {{13{1'b0}}, IR[10:8]};  // Bit_Extender bit_extender_7
  Decoder #(.enable("false"), .select(2)) decoder_3 (
    .out0(decoder_3_out0), .out1(decoder_3_out1), .out2(decoder_3_out2), .out3(decoder_3_out3), .sel(regwctl));
  assign flags_direct = decoder_1_out4 ? bit_extender_7_out : 16'bz;  // Controlled_Buffer controlled_buffer_2
  three_one_AND three_one_and_5 (.in1U(decoder_3_out3), .in3(3'b110), .out3(three_one_and_5_out3));  // open: in1D
  three_one_AND three_one_and_6 (.in1U(decoder_3_out2), .in3(3'b111), .out3(three_one_and_6_out3));  // open: in1D
  three_one_AND three_one_and_7 (.in1U(decoder_3_out1), .in3(IR[10:8]), .out3(three_one_and_7_out3));  // open: in1D
  assign RW = three_one_and_5_out3 | three_one_and_6_out3 | three_one_and_7_out3;  // OR_Gate or_7, 3 bits wide
  not not_6 (W_en, decoder_3_out0);

  assign opcode = {IR[11], IR[12], IR[13], IR[14], IR[15]};

  // Notes on the sheet:
  //   Op1
  //   Opcode /5
  //   Low Word /11
  //   Op2
  //   Op3
  //   imm5
  //   imm4
  //   imm11
  //   Immediates are controlled by immctl and immen
  //   If immen is set high, immediates lose their lowest SB to become the immediate enable bit
  //   imm8
  //   imm10
  //   imm11
  //   Imm54
  //   imm7
  //   imm7
  //   ImmEn
  //   (r6 LINK)
  //   (r7)
endmodule

module IO_display_controller (
  input  pause,
  input  clk,
  output addr,
  output [15:0] io_in,
  output [15:0] io_out,
  output [1:0] fsm_out
);

  wire not_1_out, not_2_out, not_3_out, s0_0_out;
  wire [1:0] undriven;

  not not_1 (not_1_out, fsm_out[1]);
  and s0_0 (s0_0_out, not_1_out, not_2_out);
  not not_2 (not_2_out, fsm_out[0]);
  Register #(.width(2)) register_1 (.D(undriven), .en(not_3_out), .clk(clk), .Q(fsm_out));  // open: clr
  not not_3 (not_3_out, pause);
  // AND_Gate and_1 has open pins: out=undriven[1]
  assign io_in = s0_0_out ? 16'h8000 : 16'bz;  // Controlled_Buffer controlled_buffer_1
  TTY tty_1 ();  // open: data, clk, we, clr

  // Notes on the sheet:
  //   init state, set ready
endmodule

module IO_port (
  input  rw,
  input  [15:0] cpu_in,
  input  addr,
  input  [15:0] io_in,
  input  clk,
  input  cpu_select,
  output [15:0] cpu_out,
  output [15:0] io_out
);

  wire decoder_1_out0, decoder_1_out1, not_1_out, not_2_out, not_3_out;
  wire [15:0] controlled_buffer_1_out, demultiplexer_1_out0, demultiplexer_1_out1, DR_q, multiplexer_1_out,
       SR_q;

  assign controlled_buffer_1_out = cpu_select ? cpu_in : 16'bz;  // Controlled_Buffer controlled_buffer_1
  Demultiplexer #(.enable("true"), .width(16)) demultiplexer_1 (
    .out0(demultiplexer_1_out0), .out1(demultiplexer_1_out1), .in(controlled_buffer_1_out), .sel(addr),
    .en(rw));
  assign controlled_buffer_1_out = not_1_out ? io_in : 16'bz;  // Controlled_Buffer controlled_buffer_2
  not not_1 (not_1_out, cpu_select);
  Decoder decoder_1 (.out0(decoder_1_out0), .out1(decoder_1_out1), .sel(addr), .en(rw));
  Register #(.width(16)) SR (.D(demultiplexer_1_out0), .en(decoder_1_out1), .clk(clk), .Q(SR_q));  // open: clr
  not not_2 (not_2_out, rw);
  Register #(.width(16)) DR (.D(demultiplexer_1_out1), .en(decoder_1_out0), .clk(clk), .Q(DR_q));  // open: clr
  Multiplexer #(.enable("true"), .width(16)) multiplexer_1 (
    .in0(SR_q), .in1(DR_q), .out(multiplexer_1_out), .sel(addr), .en(not_2_out));
  not not_3 (not_3_out, cpu_select);
  assign cpu_out = cpu_select ? multiplexer_1_out : 16'bz;  // Controlled_Buffer controlled_buffer_3
  assign io_out = not_3_out ? multiplexer_1_out : 16'bz;  // Controlled_Buffer controlled_buffer_4
endmodule

module MMU (
  input  [15:0] addr,
  output [3:0] io_addr,
  output io_on,
  output mem_on,
  output [15:0] memaddr
);

  and and_1 (io_on, addr[4], addr[5], addr[6], addr[7], addr[8], addr[9], addr[10], addr[11], addr[12], addr[13], addr[14], addr[15]);
  not not_1 (mem_on, io_on);

  assign io_addr = addr[3:0];
  assign memaddr = addr;
endmodule

module FourToOneMux (
  input  [1:0] selector,
  input  in1,
  input  in2,
  input  in3,
  input  in4
);

  wire and_1_out, and_2_out, and_3_out, and_4_out, not_1_out, not_2_out;

  not not_1 (not_1_out, selector[1]);
  not not_2 (not_2_out, selector[0]);
  and and_1 (and_1_out, not_2_out, in1, not_1_out);
  and and_2 (and_2_out, selector[0], in2, not_1_out);
  and and_3 (and_3_out, not_2_out, in3, selector[1]);
  and and_4 (and_4_out, selector[0], in4, selector[1]);
  // OR_Gate or_1 has open pins: in0=and_1_out, in1=and_2_out, in2=and_3_out, in3=and_4_out, out=open
endmodule

module FullAdder (
  input  inA,
  input  inB,
  input  carry_in,
  output D,
  output carry_out
);

  wire and_1_out, and_2_out, xor_1_out;

  xor xor_1 (xor_1_out, inA, inB);
  xor xor_2 (D, xor_1_out, carry_in);
  and and_1 (and_1_out, xor_1_out, carry_in);
  and and_2 (and_2_out, inA, inB);
  or or_1 (carry_out, and_1_out, and_2_out);
endmodule

module FullSubtractor (
  input  borrow_in,
  input  A,
  input  B,
  output D,
  output borrow_out,
  output difference,
  output borrow
);

  wire and_1_out, and_3_out, not_1_out, not_2_out, not_3_out, undriven, undriven_2, xor_1_out;

  xor xor_1 (xor_1_out, undriven_2, borrow_in);
  not not_1 (not_1_out, undriven_2);
  xor xor_2 (difference, A, B);
  not not_2 (not_2_out, A);
  xor xor_3 (D, undriven, xor_1_out);
  not not_3 (not_3_out, xor_1_out);
  and and_1 (and_1_out, not_1_out, borrow_in);
  and and_2 (borrow, not_2_out, B);
  and and_3 (and_3_out, not_3_out, undriven);
  or or_1 (borrow_out, and_3_out, and_1_out);
endmodule

module x16FullAdder (
  input  cin,
  input  [15:0] A,
  input  [15:0] B,
  output [15:0] D,
  output cout
);

  wire fulladder_1_carry_out, fulladder_2_carry_out, fulladder_3_carry_out, fulladder_4_carry_out,
       fulladder_5_carry_out, fulladder_6_carry_out, fulladder_7_carry_out, fulladder_8_carry_out,
       fulladder_9_carry_out, fulladder_10_carry_out, fulladder_11_carry_out, fulladder_12_carry_out,
       fulladder_13_carry_out, fulladder_14_carry_out, fulladder_15_carry_out;

  FullAdder fulladder_1 (.inA(A[0]), .inB(B[0]), .carry_in(cin), .D(D[0]), .carry_out(fulladder_1_carry_out));
  FullAdder fulladder_2 (
    .inA(A[1]), .inB(B[1]), .carry_in(fulladder_1_carry_out), .D(D[1]), .carry_out(fulladder_2_carry_out));
  FullAdder fulladder_3 (
    .inA(A[2]), .inB(B[2]), .carry_in(fulladder_2_carry_out), .D(D[2]), .carry_out(fulladder_3_carry_out));
  FullAdder fulladder_4 (
    .inA(A[3]), .inB(B[3]), .carry_in(fulladder_3_carry_out), .D(D[3]), .carry_out(fulladder_4_carry_out));
  FullAdder fulladder_5 (
    .inA(A[4]), .inB(B[4]), .carry_in(fulladder_4_carry_out), .D(D[4]), .carry_out(fulladder_5_carry_out));
  FullAdder fulladder_6 (
    .inA(A[5]), .inB(B[5]), .carry_in(fulladder_5_carry_out), .D(D[5]), .carry_out(fulladder_6_carry_out));
  FullAdder fulladder_7 (
    .inA(A[6]), .inB(B[6]), .carry_in(fulladder_6_carry_out), .D(D[6]), .carry_out(fulladder_7_carry_out));
  FullAdder fulladder_8 (
    .inA(A[7]), .inB(B[7]), .carry_in(fulladder_7_carry_out), .D(D[7]), .carry_out(fulladder_8_carry_out));
  FullAdder fulladder_9 (
    .inA(A[8]), .inB(B[8]), .carry_in(fulladder_8_carry_out), .D(D[8]), .carry_out(fulladder_9_carry_out));
  FullAdder fulladder_10 (
    .inA(A[9]), .inB(B[9]), .carry_in(fulladder_9_carry_out), .D(D[9]), .carry_out(fulladder_10_carry_out));
  FullAdder fulladder_11 (
    .inA(A[10]), .inB(B[10]), .carry_in(fulladder_10_carry_out), .D(D[10]), .carry_out(fulladder_11_carry_out));
  FullAdder fulladder_12 (
    .inA(A[11]), .inB(B[11]), .carry_in(fulladder_11_carry_out), .D(D[11]), .carry_out(fulladder_12_carry_out));
  FullAdder fulladder_13 (
    .inA(A[12]), .inB(B[12]), .carry_in(fulladder_12_carry_out), .D(D[12]), .carry_out(fulladder_13_carry_out));
  FullAdder fulladder_14 (
    .inA(A[13]), .inB(B[13]), .carry_in(fulladder_13_carry_out), .D(D[13]), .carry_out(fulladder_14_carry_out));
  FullAdder fulladder_15 (
    .inA(A[14]), .inB(B[14]), .carry_in(fulladder_14_carry_out), .D(D[14]), .carry_out(fulladder_15_carry_out));
  FullAdder fulladder_16 (.inA(A[15]), .inB(B[15]), .carry_in(fulladder_15_carry_out), .D(D[15]), .carry_out(cout));
endmodule

module FlagOut (
  input  [15:0] in16,
  output zero,
  output pos,
  output neg
);

  wire not_2_out, or_1_out;

  or or_1 (or_1_out, in16[0], in16[1], in16[2], in16[3], in16[4], in16[5], in16[6], in16[7], in16[8], in16[9], in16[10], in16[11], in16[12], in16[13], in16[14], in16[15]);
  not not_1 (zero, or_1_out);
  and and_1 (pos, or_1_out, not_2_out);
  not not_2 (not_2_out, in16[15]);

  assign neg = in16[15];
endmodule

module Eqx4 (
  input  [3:0] inA,
  input  [3:0] inB,
  output eq
);

  wire xnor_1_out, xnor_2_out, xnor_3_out, xnor_4_out;

  xnor xnor_1 (xnor_1_out, inA[0], inB[0]);
  xnor xnor_2 (xnor_2_out, inA[1], inB[1]);
  xnor xnor_3 (xnor_3_out, inA[2], inB[2]);
  xnor xnor_4 (xnor_4_out, inA[3], inB[3]);
  and and_1 (eq, xnor_1_out, xnor_2_out, xnor_3_out, xnor_4_out);
endmodule

module GPREG_5 (
  input  [15:0] D,
  input  WRITE_ENABLE,
  input  ENABLE,
  output [15:0] O
);

  wire and_1_out;

  and and_1 (and_1_out, WRITE_ENABLE, ENABLE);
  D_Flip_Flop d_ff_1 (.clk(and_1_out), .D(D[0]), .Q(O[0]));  // open: Qn, preset, reset
  D_Flip_Flop d_ff_2 (.clk(and_1_out), .D(D[1]), .Q(O[1]));  // open: Qn, preset, reset
  D_Flip_Flop d_ff_3 (.clk(and_1_out), .D(D[2]), .Q(O[2]));  // open: Qn, preset, reset
  D_Flip_Flop d_ff_4 (.clk(and_1_out), .D(D[3]), .Q(O[3]));  // open: Qn, preset, reset
  D_Flip_Flop d_ff_5 (.clk(and_1_out), .D(D[4]), .Q(O[4]));  // open: Qn, preset, reset
  D_Flip_Flop d_ff_6 (.clk(and_1_out), .D(D[5]), .Q(O[5]));  // open: Qn, preset, reset
  D_Flip_Flop d_ff_7 (.clk(and_1_out), .D(D[6]), .Q(O[6]));  // open: Qn, preset, reset
  D_Flip_Flop d_ff_8 (.clk(and_1_out), .D(D[7]), .Q(O[7]));  // open: Qn, preset, reset
  D_Flip_Flop d_ff_9 (.clk(and_1_out), .D(D[8]), .Q(O[8]));  // open: Qn, preset, reset
  D_Flip_Flop d_ff_10 (.clk(and_1_out), .D(D[9]), .Q(O[9]));  // open: Qn, preset, reset
  D_Flip_Flop d_ff_11 (.clk(and_1_out), .D(D[10]), .Q(O[10]));  // open: Qn, preset, reset
  D_Flip_Flop d_ff_12 (.clk(and_1_out), .D(D[11]), .Q(O[11]));  // open: Qn, preset, reset
  D_Flip_Flop d_ff_13 (.clk(and_1_out), .D(D[12]), .Q(O[12]));  // open: Qn, preset, reset
  D_Flip_Flop d_ff_14 (.clk(and_1_out), .D(D[13]), .Q(O[13]));  // open: Qn, preset, reset
  D_Flip_Flop d_ff_15 (.clk(and_1_out), .D(D[14]), .Q(O[14]));  // open: Qn, preset, reset
  D_Flip_Flop d_ff_16 (.clk(and_1_out), .D(D[15]), .Q(O[15]));  // open: Qn, preset, reset
endmodule

module x16Shifter (
  input  [15:0] in16,
  input  dir,
  input  ars
);

  wire and_1_out, and_2_out, and_3_out, and_4_out, and_5_out, and_6_out, and_7_out, and_8_out, and_9_out,
       and_10_out, and_11_out, and_12_out, and_13_out, and_14_out, and_15_out, and_16_out, and_17_out,
       and_18_out, and_19_out, and_20_out, and_21_out, and_22_out, and_23_out, and_24_out, and_25_out,
       and_26_out, and_27_out, and_28_out, and_29_out, and_30_out, not_1_out;
  wire [15:0] and_32_out;

  not not_1 (not_1_out, dir);
  and and_1 (and_1_out, dir, ars);
  and and_2 (and_2_out, and_1_out, and_3_out);
  and and_3 (and_3_out, in16[15], dir);
  or or_1 (and_32_out[15], and_2_out, and_4_out);
  and and_4 (and_4_out, not_1_out, in16[14]);
  and and_5 (and_5_out, in16[14], dir);
  or or_2 (and_32_out[14], and_3_out, and_6_out);
  and and_6 (and_6_out, not_1_out, in16[13]);
  and and_7 (and_7_out, in16[13], dir);
  or or_3 (and_32_out[13], and_5_out, and_8_out);
  and and_8 (and_8_out, not_1_out, in16[12]);
  and and_9 (and_9_out, in16[12], dir);
  or or_4 (and_32_out[12], and_7_out, and_10_out);
  and and_10 (and_10_out, not_1_out, in16[11]);
  and and_11 (and_11_out, in16[11], dir);
  or or_5 (and_32_out[11], and_9_out, and_12_out);
  and and_12 (and_12_out, not_1_out, in16[10]);
  and and_13 (and_13_out, in16[10], dir);
  or or_6 (and_32_out[10], and_11_out, and_14_out);
  and and_14 (and_14_out, not_1_out, in16[9]);
  and and_15 (and_15_out, in16[9], dir);
  or or_7 (and_32_out[9], and_13_out, and_16_out);
  and and_16 (and_16_out, not_1_out, in16[8]);
  or or_8 (and_32_out[8], and_15_out, and_18_out);
  and and_17 (and_17_out, in16[8], dir);
  and and_18 (and_18_out, not_1_out, in16[7]);
  and and_19 (and_19_out, in16[7], dir);
  or or_9 (and_32_out[7], and_17_out, and_20_out);
  and and_20 (and_20_out, not_1_out, in16[6]);
  or or_10 (and_32_out[6], and_19_out, and_22_out);
  and and_21 (and_21_out, in16[6], dir);
  and and_22 (and_22_out, not_1_out, in16[5]);
  and and_23 (and_23_out, in16[5], dir);
  or or_11 (and_32_out[5], and_21_out, and_24_out);
  and and_24 (and_24_out, not_1_out, in16[4]);
  or or_12 (and_32_out[4], and_23_out, and_26_out);
  and and_25 (and_25_out, in16[4], dir);
  and and_26 (and_26_out, not_1_out, in16[3]);
  and and_27 (and_27_out, in16[3], dir);
  or or_13 (and_32_out[3], and_25_out, and_28_out);
  and and_28 (and_28_out, not_1_out, in16[2]);
  and and_29 (and_29_out, in16[2], dir);
  or or_14 (and_32_out[2], and_27_out, and_30_out);
  and and_30 (and_30_out, not_1_out, in16[1]);
  or or_15 (and_32_out[1], and_29_out, and_32_out[0]);
  // AND_Gate and_31 has open pins: in0=in16[1], in1=dir, out=open
  and and_32 (and_32_out[0], not_1_out, in16[0]);
endmodule

module x16Multiplier (
  input  [15:0] A,
  input  [15:0] B,
  output [15:0] outlow16,
  output [15:0] outhigh16,
  output carryout
);

  wire x16fulladder_2_cout, x16fulladder_3_cout, x16fulladder_4_cout, x16fulladder_5_cout,
       x16fulladder_6_cout, x16fulladder_7_cout, x16fulladder_8_cout, x16fulladder_9_cout,
       x16fulladder_10_cout, x16fulladder_11_cout, x16fulladder_12_cout, x16fulladder_13_cout,
       x16fulladder_14_cout, x16fulladder_15_cout, x16fulladder_16_cout;
  wire [15:0] x16andx1_1_out16, x16andx1_2_out16, x16andx1_3_out16, x16andx1_4_out16, x16andx1_5_out16,
       x16andx1_6_out16, x16andx1_7_out16, x16andx1_8_out16, x16andx1_9_out16, x16andx1_10_out16,
       x16andx1_11_out16, x16andx1_12_out16, x16andx1_13_out16, x16andx1_14_out16, x16andx1_15_out16,
       x16andx1_16_out16, x16andx1_17_out16, x16fulladder_2_d, x16fulladder_3_d, x16fulladder_4_d,
       x16fulladder_5_d, x16fulladder_6_d, x16fulladder_7_d, x16fulladder_8_d, x16fulladder_9_d,
       x16fulladder_10_d, x16fulladder_11_d, x16fulladder_12_d, x16fulladder_13_d, x16fulladder_14_d,
       x16fulladder_15_d, x16fulladder_16_d, x16splitlast_1_o16, x16splitlast_2_o16, x16splitlast_3_o16,
       x16splitlast_4_o16, x16splitlast_5_o16, x16splitlast_6_o16, x16splitlast_7_o16, x16splitlast_8_o16,
       x16splitlast_9_o16, x16splitlast_10_o16, x16splitlast_11_o16, x16splitlast_12_o16,
       x16splitlast_13_o16, x16splitlast_14_o16, x16splitlast_15_o16, x16splitlast_16_o16;

  x16ANDx1 x16andx1_1 (.in1D(B[15]), .out16(x16andx1_1_out16));  // open: in16
  x16ANDx1 x16andx1_2 (.in1D(B[14]), .out16(x16andx1_2_out16));  // open: in16
  x16FullAdder x16fulladder_1 (
    .B(x16splitlast_1_o16), .A(x16andx1_1_out16), .D(outhigh16), .cout(carryout));  // open: cin
  x16ANDx1 x16andx1_3 (.in1D(B[13]), .out16(x16andx1_3_out16));  // open: in16
  x16FullAdder x16fulladder_2 (
    .B(x16splitlast_2_o16), .A(x16andx1_2_out16), .D(x16fulladder_2_d), .cout(x16fulladder_2_cout));  // open: cin
  x16ANDx1 x16andx1_4 (.in1D(B[12]), .in16(A), .out16(x16andx1_4_out16));
  x16FullAdder x16fulladder_3 (
    .B(x16splitlast_3_o16), .A(x16andx1_3_out16), .D(x16fulladder_3_d), .cout(x16fulladder_3_cout));  // open: cin
  x16ANDx1 x16andx1_5 (.in1D(B[11]), .in16(A), .out16(x16andx1_5_out16));
  x16SplitLast x16splitlast_1 (.ilast1(x16fulladder_2_cout), .o1(outlow16[15]), .o16(x16splitlast_1_o16));  // open: i16
  x16FullAdder x16fulladder_4 (
    .B(x16splitlast_4_o16), .A(x16andx1_4_out16), .D(x16fulladder_4_d), .cout(x16fulladder_4_cout));  // open: cin
  x16SplitLast x16splitlast_2 (
    .i16(x16fulladder_3_d), .ilast1(x16fulladder_3_cout), .o1(outlow16[14]), .o16(x16splitlast_2_o16));
  x16ANDx1 x16andx1_6 (.in1D(B[10]), .in16(A), .out16(x16andx1_6_out16));
  x16FullAdder x16fulladder_5 (
    .B(x16splitlast_5_o16), .A(x16andx1_5_out16), .D(x16fulladder_5_d), .cout(x16fulladder_5_cout));  // open: cin
  x16ANDx1 x16andx1_7 (.in1D(B[9]), .in16(A), .out16(x16andx1_7_out16));
  x16SplitLast x16splitlast_3 (
    .i16(x16fulladder_4_d), .ilast1(x16fulladder_4_cout), .o1(outlow16[13]), .o16(x16splitlast_3_o16));
  x16FullAdder x16fulladder_6 (
    .B(x16splitlast_6_o16), .A(x16andx1_6_out16), .D(x16fulladder_6_d), .cout(x16fulladder_6_cout));  // open: cin
  x16SplitLast x16splitlast_4 (
    .i16(x16fulladder_5_d), .ilast1(x16fulladder_5_cout), .o1(outlow16[12]), .o16(x16splitlast_4_o16));
  x16ANDx1 x16andx1_8 (.in1D(B[8]), .in16(A), .out16(x16andx1_8_out16));
  x16FullAdder x16fulladder_7 (
    .B(x16splitlast_7_o16), .A(x16andx1_7_out16), .D(x16fulladder_7_d), .cout(x16fulladder_7_cout));  // open: cin
  x16ANDx1 x16andx1_9 (.in1D(B[7]), .in16(A), .out16(x16andx1_9_out16));
  x16SplitLast x16splitlast_5 (
    .i16(x16fulladder_6_d), .ilast1(x16fulladder_6_cout), .o1(outlow16[11]), .o16(x16splitlast_5_o16));
  x16FullAdder x16fulladder_8 (
    .B(x16splitlast_8_o16), .A(x16andx1_8_out16), .D(x16fulladder_8_d), .cout(x16fulladder_8_cout));  // open: cin
  x16SplitLast x16splitlast_6 (
    .i16(x16fulladder_7_d), .ilast1(x16fulladder_7_cout), .o1(outlow16[10]), .o16(x16splitlast_6_o16));
  x16ANDx1 x16andx1_10 (.in1D(B[6]), .in16(A), .out16(x16andx1_10_out16));
  x16FullAdder x16fulladder_9 (
    .B(x16splitlast_9_o16), .A(x16andx1_9_out16), .D(x16fulladder_9_d), .cout(x16fulladder_9_cout));  // open: cin
  x16ANDx1 x16andx1_11 (.in1D(B[5]), .in16(A), .out16(x16andx1_11_out16));
  x16SplitLast x16splitlast_7 (
    .i16(x16fulladder_8_d), .ilast1(x16fulladder_8_cout), .o1(outlow16[9]), .o16(x16splitlast_7_o16));
  x16FullAdder x16fulladder_10 (
    .B(x16splitlast_10_o16), .A(x16andx1_10_out16), .D(x16fulladder_10_d), .cout(x16fulladder_10_cout));  // open: cin
  x16SplitLast x16splitlast_8 (
    .i16(x16fulladder_9_d), .ilast1(x16fulladder_9_cout), .o1(outlow16[8]), .o16(x16splitlast_8_o16));
  x16ANDx1 x16andx1_12 (.in1D(B[4]), .in16(A), .out16(x16andx1_12_out16));
  x16FullAdder x16fulladder_11 (
    .B(x16splitlast_11_o16), .A(x16andx1_11_out16), .D(x16fulladder_11_d), .cout(x16fulladder_11_cout));  // open: cin
  x16ANDx1 x16andx1_13 (.in16(A), .out16(x16andx1_13_out16));  // open: in1D
  x16SplitLast x16splitlast_9 (.ilast1(x16fulladder_10_cout), .o1(outlow16[7]), .o16(x16splitlast_9_o16));  // open: i16
  x16FullAdder x16fulladder_12 (
    .B(x16splitlast_12_o16), .A(x16andx1_12_out16), .D(x16fulladder_12_d), .cout(x16fulladder_12_cout));  // open: cin
  x16SplitLast x16splitlast_10 (
    .i16(x16fulladder_11_d), .ilast1(x16fulladder_11_cout), .o1(outlow16[6]), .o16(x16splitlast_10_o16));
  x16ANDx1 x16andx1_14 (.in1D(B[3]), .in16(A), .out16(x16andx1_14_out16));
  x16FullAdder x16fulladder_13 (
    .B(x16splitlast_13_o16), .A(x16andx1_13_out16), .D(x16fulladder_13_d), .cout(x16fulladder_13_cout));  // open: cin
  x16ANDx1 x16andx1_15 (.in1D(B[2]), .in16(A), .out16(x16andx1_15_out16));
  x16SplitLast x16splitlast_11 (
    .i16(x16fulladder_12_d), .ilast1(x16fulladder_12_cout), .o1(outlow16[5]), .o16(x16splitlast_11_o16));
  x16FullAdder x16fulladder_14 (
    .B(x16splitlast_14_o16), .A(x16andx1_14_out16), .D(x16fulladder_14_d), .cout(x16fulladder_14_cout));  // open: cin
  x16SplitLast x16splitlast_12 (
    .i16(x16fulladder_13_d), .ilast1(x16fulladder_13_cout), .o1(outlow16[4]), .o16(x16splitlast_12_o16));
  x16ANDx1 x16andx1_16 (.in1D(B[1]), .in16(A), .out16(x16andx1_16_out16));
  x16FullAdder x16fulladder_15 (
    .B(x16splitlast_16_o16), .A(x16andx1_15_out16), .D(x16fulladder_15_d), .cout(x16fulladder_15_cout));  // open: cin
  x16SplitLast x16splitlast_13 (
    .i16(x16fulladder_14_d), .ilast1(x16fulladder_14_cout), .o1(outlow16[3]), .o16(x16splitlast_13_o16));
  x16FullAdder x16fulladder_16 (
    .B(x16splitlast_15_o16), .A(x16andx1_16_out16), .D(x16fulladder_16_d), .cout(x16fulladder_16_cout));  // open: cin
  x16SplitLast x16splitlast_14 (
    .i16(x16fulladder_15_d), .ilast1(x16fulladder_15_cout), .o1(outlow16[2]), .o16(x16splitlast_14_o16));
  x16ANDx1 x16andx1_17 (.in1D(B[0]), .in16(A), .out16(x16andx1_17_out16));
  x16SplitLast x16splitlast_15 (.i16(x16andx1_17_out16), .o1(outlow16[0]), .o16(x16splitlast_15_o16));  // open: ilast1
  x16SplitLast x16splitlast_16 (
    .i16(x16fulladder_16_d), .ilast1(x16fulladder_16_cout), .o1(outlow16[1]), .o16(x16splitlast_16_o16));
endmodule

module x16ANDx1 (
  input  in1D,
  input  [15:0] in16,
  output [15:0] out16
);

  and and_1 (out16[0], in1D, in16[0]);
  and and_2 (out16[1], in1D, in16[1]);
  and and_3 (out16[2], in1D, in16[2]);
  and and_4 (out16[3], in1D, in16[3]);
  and and_5 (out16[4], in1D, in16[4]);
  and and_6 (out16[5], in1D, in16[5]);
  and and_7 (out16[6], in1D, in16[6]);
  and and_8 (out16[7], in1D, in16[7]);
  and and_9 (out16[8], in1D, in16[8]);
  and and_10 (out16[9], in1D, in16[9]);
  and and_11 (out16[10], in1D, in16[10]);
  and and_12 (out16[11], in1D, in16[11]);
  and and_13 (out16[12], in1D, in16[12]);
  and and_14 (out16[13], in1D, in16[13]);
  and and_15 (out16[14], in1D, in16[14]);
  and and_16 (out16[15], in1D, in16[15]);
endmodule

module x16SplitLast (
  input  [15:0] i16,
  input  ilast1,
  output o1,
  output [15:0] o16
);


  assign o1 = i16[0];
  assign o16 = {ilast1, i16[15:1]};
endmodule

module demux (
  input  [1:0] sel,
  output out1,
  output out2,
  output out3,
  output out4
);

  wire not_1_out, not_2_out;

  not not_1 (not_1_out, sel[1]);
  not not_2 (not_2_out, sel[0]);
  and and_1 (out1, not_2_out, 1'b1, not_1_out);
  and and_2 (out2, sel[0], 1'b1, not_1_out);
  and and_3 (out3, not_2_out, 1'b1, sel[1]);
  and and_4 (out4, sel[0], 1'b1, sel[1]);

  // Notes on the sheet:
  //   constant 1
endmodule
